// Logisim project T3.circ as structural Verilog: 1 circuit, main circuit main
module main (
  input  SET,
  input  INN,
  output OUTT
);

  wire and_1_out, and_2_out, and_3_out, and_4_out, clock_1_out, CS0, CS1, CS2, not_1_out, not_2_out,
       not_3_out, not_4_out, or_1_out;

  not not_1 (not_1_out, INN);
  not not_2 (not_2_out, CS2);
  not not_3 (not_3_out, CS1);
  not not_4 (not_4_out, CS0);
  and and_1 (and_1_out, CS2, CS0);
  and and_2 (and_2_out, CS2, INN, CS0);
  and and_3 (and_3_out, CS2, not_1_out, not_4_out);
  and and_4 (and_4_out, not_1_out, not_2_out, not_3_out, not_4_out);
  or or_1 (or_1_out, and_4_out, and_1_out);
  Clock clock_1 (.out(clock_1_out));
  or or_2 (OUTT, and_2_out, and_3_out);
  Register #(.width(1)) register_1 (.D(1'b1), .en(SET), .clk(clock_1_out), .Q(CS2));  // open: clr
  Register #(.width(1)) register_2 (.D(or_1_out), .clk(clock_1_out), .Q(CS1));  // open: en, clr
  Register #(.width(1)) register_3 (.D(INN), .clk(clock_1_out), .Q(CS0));  // open: en, clr
endmodule
