// Logisim project ex5_1.circ as structural Verilog: 2 circuits, main circuit Running_LED
module Running_LED (
  input  [7:0] INITIAL_LED,
  input  RST,
  output [7:0] OUT_LED
);

  wire clock_1_out, comparator_1_gt;
  wire [7:0] adder_1_out, multiplexer_1_out, register_1_q, register_2_q, ro1_1_out_2;

  Clock clock_1 (.out(clock_1_out));
  LED led_1 (.in(OUT_LED[7]));
  LED led_2 (.in(OUT_LED[6]));
  Multiplexer #(.width(8)) multiplexer_1 (.in0(OUT_LED), .in1(INITIAL_LED), .out(multiplexer_1_out), .sel(RST));
  LED led_3 (.in(OUT_LED[5]));
  Register register_1 (.D(multiplexer_1_out), .clk(clock_1_out), .Q(register_1_q));  // open: en, clr
  Adder adder_1 (.a(register_2_q), .b(8'h1), .out(adder_1_out));  // open: cin, cout
  LED led_4 (.in(OUT_LED[4]));
  Register register_2 (.D(adder_1_out), .clk(clock_1_out), .Q(register_2_q), .clr(RST));  // open: en
  LED led_5 (.in(OUT_LED[3]));
  LED led_6 (.in(OUT_LED[2]));
  ro1 ro1_1 (.in_1(register_1_q), .out_2(ro1_1_out_2));
  LED led_7 (.in(OUT_LED[1]));
  Multiplexer #(.width(8)) multiplexer_2 (.in0(ro1_1_out_2), .in1(register_1_q), .out(OUT_LED), .sel(comparator_1_gt));
  Comparator comparator_1 (.a(register_2_q), .b(8'h8), .gt(comparator_1_gt));  // open: eq, lt
  LED led_8 (.in(OUT_LED[0]));

  // Notes on the sheet:
  //   PUT CIRCUITS HERE
endmodule

module ro1 (
  input  [7:0] in_1,
  output [7:0] out_2
);


  assign out_2 = {in_1[0], in_1[7:1]};
endmodule
