// Logisim project ex3_test.circ as structural Verilog: 1 circuit, main circuit main
module main (
  output [7:0] out_1,
  output OUT1,
  output OUT2,
  output [8:0] OUT3,
  output [8:0] OUT4,
  output halt,
  output [7:0] out_7
);

  wire clock_1_out;
  wire [7:0] adder_1_out;

  Clock clock_1 (.out(clock_1_out));
  Adder adder_1 (.a(8'h1), .b(out_1), .out(adder_1_out));  // open: cin, cout
  Register register_1 (.D(adder_1_out), .clk(clock_1_out), .Q(out_1));  // open: en, clr
  Comparator comparator_1 (.a(out_1), .b(8'hd), .eq(halt));  // open: gt, lt
  ROM rom_1 (.addr(out_1), .data(out_7));
  Split split_1 (.IN1(out_7), .OUT1(OUT1), .OUT2(OUT2), .OUT3(OUT3), .OUT4(OUT4));

  // Other names for the same wires on the sheet: IN1[7:0] = out_7; Test[7:0] = out_1

  // Notes on the sheet:
  //   contents of rom_1 (hex, n*v repeats v):
  //   1 80 81 ff f0 ef fd ed 87 96 57 aa d 2f
  //   Your Split circuit must fit here!
  //   There should be no red or blue wires, and the result should not be all X's
endmodule
