// Logisim project ex2.circ as structural Verilog: 1 circuit, main circuit main
module main (
  input  clk,
  input  rst,
  input  pc_update,
  input  [31:0] new_addr,
  output [31:0] current_addr
);

  wire [1:0] and_1_out;
  wire [31:0] adder_1_out, multiplexer_1_out;

  assign and_1_out = 2'b00 & new_addr[1:0];  // AND_Gate and_1, 2 bits wide
  Adder #(.width(32)) adder_1 (.a(32'h4), .b(current_addr), .out(adder_1_out));  // open: cin, cout
  Multiplexer #(.width(32)) multiplexer_1 (
    .in0(adder_1_out), .in1({new_addr[31:2], and_1_out}), .out(multiplexer_1_out), .sel(pc_update));
  Register #(.width(32)) register_1 (.D(multiplexer_1_out), .clk(clk), .Q(current_addr), .clr(rst));  // open: en
endmodule
