// Logisim project proj_2_1_top.circ as structural Verilog: 7 circuits, main circuit testbench
module TOP (
  input  clk,
  input  rst,
  input  [31:0] inst,
  output [31:0] inst_addr,
  output mem_wen,
  output [31:0] mem_din,
  output [31:0] mem_dout,
  output [31:0] mem_addr,
  output control_en,
  output [31:0] control_pc,
  output wb_en,
  output [4:0] wb_addr,
  output [31:0] wb_data
);

  wire BrEq, BrLT, BrUn, BSel, comparator_1_lt, comparator_2_lt, control_1_control_en, control_1_memrw,
       control_1_reg_en, mem_ren, SH;
  wire [0:0] multiplexer_7_out;
  wire [1:0] ASel, WBSel;
  wire [2:0] Imm_sel;
  wire [3:0] ALUSel;
  wire [4:0] multiplexer_5_out;
  wire [31:0] adder_1_out, adder_2_out, alu_result, and_1_out, bit_extender_1_out, bit_extender_2_out,
       bit_extender_3_out, dmem_1_readdata, Gen_Imm, multiplexer_2_out, multiplexer_3_out, multiplexer_4_out,
       multiplexer_6_out, multiplexer_8_out, multiplexer_9_out, multiplexer_10_out, r1, r2, undriven,
       undriven_2, undriven_3;

  Comparator #(.width(32)) comparator_1 (.a(r1), .b(r2), .eq(BrEq), .lt(comparator_1_lt));  // open: gt
  Comparator #(.mode("unsigned"), .width(32)) comparator_2 (.a(r1), .b(r2), .lt(comparator_2_lt));  // open: gt, eq
  Multiplexer multiplexer_1 (.in0(comparator_1_lt), .in1(comparator_2_lt), .out(BrLT), .sel(BrUn));
  Adder #(.width(32)) adder_1 (.a(32'h4), .b(inst_addr), .out(adder_1_out));  // open: cin, cout
  Multiplexer #(.width(32)) multiplexer_2 (
    .in0(adder_1_out), .in1({alu_result[31:1], 1'b0}), .out(multiplexer_2_out), .sel(control_en));
  Multiplexer #(.select(2), .width(32)) multiplexer_3 (
    .in0(r1), .in1(inst_addr), .in2({32{1'b0}}), .out(multiplexer_3_out), .sel(ASel));  // open: in3
  Multiplexer #(.width(32)) multiplexer_4 (.in0(r2), .in1(Gen_Imm), .out(multiplexer_4_out), .sel(BSel));
  imm_gen imm_gen_1 (.Inst(inst), .Imm_sel(Imm_sel), .Imm(Gen_Imm));
  regfile regfile_1 (
    .Read_Register_1_rs1(inst[19:15]), .Read_Register_2_rs2(inst[24:20]), .Write_Register_rd(wb_addr),
    .Write_Data(wb_data), .Write_Enable(wb_en), .Clock(clk), .RST(rst), .Read_Data_1(r1), .Read_Data_2(r2));  // open: ra, sp, t0, t1, t2, s0, s1, a0
  Register #(.width(32)) PC (.D(multiplexer_2_out), .clk(clk), .Q(inst_addr), .clr(rst));  // open: en
  ALU alu_1 (.A(multiplexer_3_out), .B(multiplexer_4_out), .ALUSel(ALUSel), .Result(alu_result));
  Multiplexer #(.width(5)) multiplexer_5 (.in0({5{1'b0}}), .in1(inst[11:7]), .out(multiplexer_5_out), .sel(wb_en));
  Multiplexer #(.width(32)) multiplexer_6 (
    .in0({32{1'b0}}), .in1(alu_result), .out(multiplexer_6_out), .sel(control_en));
  DMEM dmem_1 (
    .mem_ren(mem_ren), .WriteAddr(alu_result), .WriteData(mem_din), .MemRW(mem_wen), .clk(clk), .rst(rst),
    .is_sh(SH), .ReadData(dmem_1_readdata));
  control control_1 (
    .Instruction(inst), .BrEq(BrEq), .BrLT(BrLT), .ImmSel(Imm_sel), .control_en(control_1_control_en),
    .ASel(ASel), .BSel(BSel), .ALUSel(ALUSel), .MemRW(control_1_memrw), .reg_en(control_1_reg_en),
    .WBSel(WBSel), .mem_ren(mem_ren), .if_sh(SH));
  Multiplexer #(.width(32)) multiplexer_7 (
    .in0(multiplexer_6_out), .in1({32{1'b0}}), .out({control_pc[31:1], multiplexer_7_out[0]}), .sel(rst));
  assign bit_extender_1_out = {{31{mem_wen}}, mem_wen};  // Bit_Extender bit_extender_1
  assign bit_extender_2_out = {{16{dmem_1_readdata[15]}}, dmem_1_readdata[15:0]};  // Bit_Extender bit_extender_2
  Bit_Extender #(.in_width(32), .out_width(32)) bit_extender_3 (.in(dmem_1_readdata), .out(bit_extender_3_out));
  assign and_1_out = bit_extender_1_out & r2;  // AND_Gate and_1, 32 bits wide
  Multiplexer #(.select(3), .width(32)) multiplexer_8 (
    .in0(undriven), .in1(bit_extender_2_out), .in2(bit_extender_3_out), .in3(undriven_2), .in4(undriven_3),
    .in7({32{1'b0}}), .out(multiplexer_8_out), .sel(inst[14:12]));  // open: in5, in6
  Adder #(.width(32)) adder_2 (.a(inst_addr), .b(32'h4), .out(adder_2_out));  // open: cin, cout
  Multiplexer #(.width(32)) multiplexer_9 (.in0({32{1'b0}}), .in1(alu_result), .out(multiplexer_9_out), .sel(mem_ren));
  Multiplexer #(.select(2), .width(32)) multiplexer_10 (
    .in0(multiplexer_8_out), .in1(alu_result), .in2(adder_2_out), .in3({32{1'b0}}), .out(multiplexer_10_out),
    .sel(WBSel));
  Multiplexer multiplexer_11 (.in0(control_1_control_en), .in1(1'b0), .out(control_en), .sel(rst));
  Multiplexer #(.width(32)) multiplexer_12 (.in0(and_1_out), .in1({32{1'b0}}), .out(mem_din), .sel(rst));
  Multiplexer #(.width(5)) multiplexer_13 (.in0(multiplexer_5_out), .in1({5{1'b0}}), .out(wb_addr), .sel(rst));
  Multiplexer multiplexer_14 (.in0(control_1_memrw), .in1(1'b0), .out(mem_wen), .sel(rst));
  Multiplexer multiplexer_15 (.in0(control_1_reg_en), .in1(1'b0), .out(wb_en), .sel(rst));
  Multiplexer #(.width(32)) multiplexer_16 (.in0(dmem_1_readdata), .in1({32{1'b0}}), .out(mem_dout), .sel(rst));
  Multiplexer #(.width(32)) multiplexer_17 (.in0(multiplexer_10_out), .in1({32{1'b0}}), .out(wb_data), .sel(rst));
  Multiplexer #(.width(32)) multiplexer_18 (.in0(multiplexer_9_out), .in1({32{1'b0}}), .out(mem_addr), .sel(rst));

  assign control_pc[0] = 1'b0;

  // Other names for the same wires on the sheet: Opcode[6:0] = inst[6:0]; funct3[2:0] = inst[14:12];
  //   write_rs1_addr[4:0] = inst[19:15]; write_rs2_addr[4:0] = inst[24:20]; funct7[6:0] = inst[31:25]

  // Notes on the sheet:
  //   B type comparator
  //   unsigned comparator
  //   pcsel=1,alu result will be suitable for auipc
  //   DON'T TOUCH!
  //   enable writing value to pc
endmodule

module testbench (
  input  rst,
  output [5:0] out_2,
  output out_3,
  output halt,
  output [31:0] out_5,
  output [31:0] mem_dout,
  output [31:0] mem_addr,
  output out_8,
  output [31:0] out_9,
  output out_10,
  output [4:0] out_11,
  output [31:0] out_12
);

  wire and_1_out, carry, clk, not_1_out, not_2_out, por_1_out, rst_t;
  wire [31:0] inst, inst_addr;

  not not_1 (not_1_out, inst[2]);
  not not_2 (not_2_out, inst[3]);
  POR por_1 (.out(por_1_out));
  TOP top_1 (
    .clk(clk), .rst(rst_t), .inst(inst), .inst_addr(inst_addr), .mem_wen(out_3), .mem_din(out_5),
    .mem_dout(mem_dout), .mem_addr(mem_addr), .control_en(out_8), .control_pc(out_9), .wb_en(out_10),
    .wb_addr(out_11), .wb_data(out_12));
  Clock clock_1 (.out(clk));
  or or_1 (rst_t, rst, por_1_out);
  and and_1 (and_1_out, inst[0], inst[1], not_1_out, not_2_out, inst[4], inst[5], inst[6]);
  or or_2 (halt, and_1_out, carry);
  Counter #(.max('h3f), .width(6)) counter_1 (
    .clr(rst_t), .up(1'b1), .count(1'b1), .clk(clk), .carry(carry), .Q(out_2));  // open: load, D
  // ROM #(.line("quad"), .misaligned("true")) inst_mem: pin names not known; wires that end beside it: inst_addr[7:0], inst[7:0], inst[15:8], inst[23:16], inst[31:24]
  // Probe on inst

  // Other names for the same wires on the sheet: control_en = out_8; control_pc[31:0] = out_9; mem_din[31:0] = out_5;
  //   mem_wen = out_3; wb_addr[4:0] = out_11; wb_data[31:0] = out_12; wb_en = out_10

  // Notes on the sheet:
  //   DON'T TOUCH!
  //   contents of inst_mem (hex, n*v repeats v):
  //   93 0 d0 ff 13 1 50 0 23 10 11 0 83 11 11
  //   you can write any instruction in
endmodule

module regfile (
  input  [4:0] Read_Register_1_rs1,
  input  [4:0] Read_Register_2_rs2,
  input  [4:0] Write_Register_rd,
  input  [31:0] Write_Data,
  input  Write_Enable,
  input  Clock,
  input  RST,
  output [31:0] ra,
  output [31:0] sp,
  output [31:0] t0,
  output [31:0] t1,
  output [31:0] t2,
  output [31:0] s0,
  output [31:0] s1,
  output [31:0] a0,
  output [31:0] Read_Data_1,
  output [31:0] Read_Data_2
);

  wire demultiplexer_1_out1, demultiplexer_1_out2, demultiplexer_1_out3, demultiplexer_1_out4,
       demultiplexer_1_out5, demultiplexer_1_out6, demultiplexer_1_out7, demultiplexer_1_out8,
       demultiplexer_1_out9, demultiplexer_1_out10, demultiplexer_1_out11, demultiplexer_1_out12,
       demultiplexer_1_out13, demultiplexer_1_out14, demultiplexer_1_out15, demultiplexer_1_out16,
       demultiplexer_1_out17, demultiplexer_1_out18, demultiplexer_1_out19, demultiplexer_1_out20,
       demultiplexer_1_out21, demultiplexer_1_out22, demultiplexer_1_out23, demultiplexer_1_out24,
       demultiplexer_1_out25, demultiplexer_1_out26, demultiplexer_1_out27, demultiplexer_1_out28,
       demultiplexer_1_out29, demultiplexer_1_out30, demultiplexer_1_out31;
  wire [31:0] a1, a2, a3, a4, a5, a6, a7, gp, s2, s3, s4, s5, s6, s7, s8, s9, s10, s11, t3, t4, t5, t6, tp;

  Demultiplexer #(.select(5)) demultiplexer_1 (
    .out1(demultiplexer_1_out1), .out2(demultiplexer_1_out2), .out3(demultiplexer_1_out3),
    .out4(demultiplexer_1_out4), .out5(demultiplexer_1_out5), .out6(demultiplexer_1_out6),
    .out7(demultiplexer_1_out7), .out8(demultiplexer_1_out8), .out9(demultiplexer_1_out9),
    .out10(demultiplexer_1_out10), .out11(demultiplexer_1_out11), .out12(demultiplexer_1_out12),
    .out13(demultiplexer_1_out13), .out14(demultiplexer_1_out14), .out15(demultiplexer_1_out15),
    .out16(demultiplexer_1_out16), .out17(demultiplexer_1_out17), .out18(demultiplexer_1_out18),
    .out19(demultiplexer_1_out19), .out20(demultiplexer_1_out20), .out21(demultiplexer_1_out21),
    .out22(demultiplexer_1_out22), .out23(demultiplexer_1_out23), .out24(demultiplexer_1_out24),
    .out25(demultiplexer_1_out25), .out26(demultiplexer_1_out26), .out27(demultiplexer_1_out27),
    .out28(demultiplexer_1_out28), .out29(demultiplexer_1_out29), .out30(demultiplexer_1_out30),
    .out31(demultiplexer_1_out31), .in(Write_Enable), .sel(Write_Register_rd));  // open: out0
  Register #(.width(32)) register_1 (.D(Write_Data), .en(demultiplexer_1_out1), .clk(Clock), .Q(ra), .clr(RST));
  Register #(.width(32)) register_2 (.D(Write_Data), .en(demultiplexer_1_out2), .clk(Clock), .Q(sp), .clr(RST));
  Register #(.width(32)) register_3 (.D(Write_Data), .en(demultiplexer_1_out3), .clk(Clock), .Q(gp), .clr(RST));
  Register #(.width(32)) register_4 (.D(Write_Data), .en(demultiplexer_1_out4), .clk(Clock), .Q(tp), .clr(RST));
  Register #(.width(32)) register_5 (.D(Write_Data), .en(demultiplexer_1_out5), .clk(Clock), .Q(t0), .clr(RST));
  Register #(.width(32)) register_6 (.D(Write_Data), .en(demultiplexer_1_out6), .clk(Clock), .Q(t1), .clr(RST));
  Register #(.width(32)) register_7 (.D(Write_Data), .en(demultiplexer_1_out7), .clk(Clock), .Q(t2), .clr(RST));
  Register #(.width(32)) register_8 (.D(Write_Data), .en(demultiplexer_1_out8), .clk(Clock), .Q(s0), .clr(RST));
  Register #(.width(32)) register_9 (.D(Write_Data), .en(demultiplexer_1_out9), .clk(Clock), .Q(s1), .clr(RST));
  Register #(.width(32)) register_10 (.D(Write_Data), .en(demultiplexer_1_out10), .clk(Clock), .Q(a0), .clr(RST));
  Register #(.width(32)) register_11 (.D(Write_Data), .en(demultiplexer_1_out11), .clk(Clock), .Q(a1), .clr(RST));
  Register #(.width(32)) register_12 (.D(Write_Data), .en(demultiplexer_1_out12), .clk(Clock), .Q(a2), .clr(RST));
  Register #(.width(32)) register_13 (.D(Write_Data), .en(demultiplexer_1_out13), .clk(Clock), .Q(a3), .clr(RST));
  Register #(.width(32)) register_14 (.D(Write_Data), .en(demultiplexer_1_out14), .clk(Clock), .Q(a4), .clr(RST));
  Register #(.width(32)) register_15 (.D(Write_Data), .en(demultiplexer_1_out15), .clk(Clock), .Q(a5), .clr(RST));
  Register #(.width(32)) register_16 (.D(Write_Data), .en(demultiplexer_1_out16), .clk(Clock), .Q(a6), .clr(RST));
  Register #(.width(32)) register_17 (.D(Write_Data), .en(demultiplexer_1_out17), .clk(Clock), .Q(a7), .clr(RST));
  Register #(.width(32)) register_18 (.D(Write_Data), .en(demultiplexer_1_out18), .clk(Clock), .Q(s2), .clr(RST));
  Register #(.width(32)) register_19 (.D(Write_Data), .en(demultiplexer_1_out19), .clk(Clock), .Q(s3), .clr(RST));
  Register #(.width(32)) register_20 (.D(Write_Data), .en(demultiplexer_1_out20), .clk(Clock), .Q(s4), .clr(RST));
  Register #(.width(32)) register_21 (.D(Write_Data), .en(demultiplexer_1_out21), .clk(Clock), .Q(s5), .clr(RST));
  Register #(.width(32)) register_22 (.D(Write_Data), .en(demultiplexer_1_out22), .clk(Clock), .Q(s6), .clr(RST));
  Register #(.width(32)) register_23 (.D(Write_Data), .en(demultiplexer_1_out23), .clk(Clock), .Q(s7), .clr(RST));
  Register #(.width(32)) register_24 (.D(Write_Data), .en(demultiplexer_1_out24), .clk(Clock), .Q(s8), .clr(RST));
  Register #(.width(32)) register_25 (.D(Write_Data), .en(demultiplexer_1_out25), .clk(Clock), .Q(s9), .clr(RST));
  Register #(.width(32)) register_26 (.D(Write_Data), .en(demultiplexer_1_out26), .clk(Clock), .Q(s10), .clr(RST));
  Register #(.width(32)) register_27 (.D(Write_Data), .en(demultiplexer_1_out27), .clk(Clock), .Q(s11), .clr(RST));
  Register #(.width(32)) register_28 (.D(Write_Data), .en(demultiplexer_1_out28), .clk(Clock), .Q(t3), .clr(RST));
  Register #(.width(32)) register_29 (.D(Write_Data), .en(demultiplexer_1_out29), .clk(Clock), .Q(t4), .clr(RST));
  Register #(.width(32)) register_30 (.D(Write_Data), .en(demultiplexer_1_out30), .clk(Clock), .Q(t5), .clr(RST));
  Register #(.width(32)) register_31 (.D(Write_Data), .en(demultiplexer_1_out31), .clk(Clock), .Q(t6), .clr(RST));
  Multiplexer #(.select(5), .width(32)) multiplexer_1 (
    .in0({32{1'b0}}), .in1(ra), .in2(sp), .in3(gp), .in4(tp), .in5(t0), .in6(t1), .in7(t2), .in8(s0),
    .in9(s1), .in10(a0), .in11(a1), .in12(a2), .in13(a3), .in14(a4), .in15(a5), .in16(a6), .in17(a7),
    .in18(s2), .in19(s3), .in20(s4), .in21(s5), .in22(s6), .in23(s7), .in24(s8), .in25(s9), .in26(s10),
    .in27(s11), .in28(t3), .in29(t4), .in30(t5), .in31(t6), .out(Read_Data_1), .sel(Read_Register_1_rs1));
  Multiplexer #(.select(5), .width(32)) multiplexer_2 (
    .in0({32{1'b0}}), .in1(ra), .in2(sp), .in3(gp), .in4(tp), .in5(t0), .in6(t1), .in7(t2), .in8(s0),
    .in9(s1), .in10(a0), .in11(a1), .in12(a2), .in13(a3), .in14(a4), .in15(a5), .in16(a6), .in17(a7),
    .in18(s2), .in19(s3), .in20(s4), .in21(s5), .in22(s6), .in23(s7), .in24(s8), .in25(s9), .in26(s10),
    .in27(s11), .in28(t3), .in29(t4), .in30(t5), .in31(t6), .out(Read_Data_2), .sel(Read_Register_2_rs2));

  // Other names for the same wires on the sheet: clk = Clock; read_data1[31:0] = Read_Data_1;
  //   read_data2[31:0] = Read_Data_2; read_reg1[4:0] = Read_Register_1_rs1; read_reg2[4:0] = Read_Register_2_rs2;
  //   write_en = Write_Enable; write_reg[4:0] = Write_Register_rd
endmodule

module DMEM (
  input  mem_ren,
  input  [31:0] WriteAddr,
  input  [31:0] WriteData,
  input  MemRW,
  input  clk,
  input  rst,
  input  is_sh,
  output [31:0] ReadData
);

  wire MemRW00, MemRW01, MemRW10, MemRW11, multiplexer_1_out, multiplexer_2_out, multiplexer_3_out,
       multiplexer_4_out, not_1_out;
  wire [7:0] multiplexer_9_out, multiplexer_10_out, multiplexer_11_out, multiplexer_12_out, out_1, out_2,
       out_3, out_4, WriteData00, WriteData01, WriteData10, WriteData11;
  wire [31:0] WriteAddr00, WriteAddr01, WriteAddr1, WriteAddr2, WriteAddr3, WriteAddr10, WriteAddr11;

  Multiplexer #(.select(2)) multiplexer_1 (
    .in0(1'b1), .in1(1'b0), .in2(1'b0), .in3(1'b1), .out(multiplexer_1_out), .sel(WriteAddr[1:0]));
  Multiplexer #(.select(2)) multiplexer_2 (
    .in0(1'b1), .in1(1'b1), .in2(1'b0), .in3(1'b0), .out(multiplexer_2_out), .sel(WriteAddr[1:0]));
  Multiplexer #(.select(2)) multiplexer_3 (
    .in0(1'b0), .in1(1'b1), .in2(1'b1), .in3(1'b0), .out(multiplexer_3_out), .sel(WriteAddr[1:0]));
  Multiplexer #(.select(2)) multiplexer_4 (
    .in0(1'b0), .in1(1'b0), .in2(1'b1), .in3(1'b1), .out(multiplexer_4_out), .sel(WriteAddr[1:0]));
  RAM #(.addrWidth(16), .asyncread("true"), .clearpin("true")) ram_1 (
    .addr(WriteAddr00[15:0]), .we(MemRW00), .oe(mem_ren), .clk(clk), .din(WriteData00), .dout(out_1),
    .clr(rst));
  Multiplexer multiplexer_5 (.in0(multiplexer_1_out), .in1(MemRW), .out(MemRW00), .sel(not_1_out));
  Multiplexer multiplexer_6 (.in0(multiplexer_2_out), .in1(MemRW), .out(MemRW01), .sel(not_1_out));
  Multiplexer multiplexer_7 (.in0(multiplexer_4_out), .in1(MemRW), .out(MemRW11), .sel(not_1_out));
  not not_1 (not_1_out, is_sh);
  Multiplexer multiplexer_8 (.in0(multiplexer_3_out), .in1(MemRW), .out(MemRW10), .sel(not_1_out));
  Adder #(.width(32)) adder_1 (.a(WriteAddr), .b(32'h1), .out(WriteAddr1));  // open: cin, cout
  Multiplexer #(.select(2), .width(8)) multiplexer_9 (
    .in0(out_1), .in1(out_2), .in2(out_3), .in3(out_4), .out(multiplexer_9_out), .sel(WriteAddr[1:0]));
  Multiplexer #(.select(2), .width(8)) multiplexer_10 (
    .in0(out_2), .in1(out_3), .in2(out_4), .in3(out_1), .out(multiplexer_10_out), .sel(WriteAddr[1:0]));
  Multiplexer #(.select(2), .width(8)) multiplexer_11 (
    .in0(out_3), .in1(out_4), .in2(out_1), .in3(out_2), .out(multiplexer_11_out), .sel(WriteAddr[1:0]));
  Multiplexer #(.select(2), .width(8)) multiplexer_12 (
    .in0(out_4), .in1(out_1), .in2(out_2), .in3(out_3), .out(multiplexer_12_out), .sel(WriteAddr[1:0]));
  Multiplexer #(.select(2), .width(32)) multiplexer_13 (
    .in0(WriteAddr), .in1(WriteAddr3), .in2(WriteAddr2), .in3(WriteAddr1), .out(WriteAddr00),
    .sel(WriteAddr[1:0]));
  Multiplexer #(.select(2), .width(32)) multiplexer_14 (
    .in0(WriteAddr1), .in1(WriteAddr), .in2(WriteAddr3), .in3(WriteAddr2), .out(WriteAddr01),
    .sel(WriteAddr[1:0]));
  Multiplexer #(.select(2), .width(32)) multiplexer_15 (
    .in0(WriteAddr2), .in1(WriteAddr1), .in2(WriteAddr), .in3(WriteAddr3), .out(WriteAddr10),
    .sel(WriteAddr[1:0]));
  Multiplexer #(.select(2), .width(32)) multiplexer_16 (
    .in0(WriteAddr3), .in1(WriteAddr2), .in2(WriteAddr1), .in3(WriteAddr), .out(WriteAddr11),
    .sel(WriteAddr[1:0]));
  RAM #(.addrWidth(16), .asyncread("true"), .clearpin("true")) meme (
    .addr(WriteAddr01[15:0]), .we(MemRW01), .oe(mem_ren), .clk(clk), .din(WriteData01), .dout(out_2),
    .clr(rst));
  Adder #(.width(32)) adder_2 (.a(WriteAddr1), .b(32'h1), .out(WriteAddr2));  // open: cin, cout
  Adder #(.width(32)) adder_3 (.a(WriteAddr2), .b(32'h1), .out(WriteAddr3));  // open: cin, cout
  Multiplexer #(.width(32)) multiplexer_17 (
    .in0({32{1'b0}}), .in1({multiplexer_12_out, multiplexer_11_out, multiplexer_10_out, multiplexer_9_out}),
    .out(ReadData), .sel(mem_ren));
  Multiplexer #(.select(2), .width(8)) multiplexer_18 (
    .in0(WriteData[7:0]), .in1(WriteData[31:24]), .in2(WriteData[23:16]), .in3(WriteData[15:8]),
    .out(WriteData00), .sel(WriteAddr[1:0]));
  Multiplexer #(.select(2), .width(8)) multiplexer_19 (
    .in0(WriteData[15:8]), .in1(WriteData[7:0]), .in2(WriteData[31:24]), .in3(WriteData[23:16]),
    .out(WriteData01), .sel(WriteAddr[1:0]));
  Multiplexer #(.select(2), .width(8)) multiplexer_20 (
    .in0(WriteData[23:16]), .in1(WriteData[15:8]), .in2(WriteData[7:0]), .in3(WriteData[31:24]),
    .out(WriteData10), .sel(WriteAddr[1:0]));
  Multiplexer #(.select(2), .width(8)) multiplexer_21 (
    .in0(WriteData[31:24]), .in1(WriteData[23:16]), .in2(WriteData[15:8]), .in3(WriteData[7:0]),
    .out(WriteData11), .sel(WriteAddr[1:0]));
  RAM #(.addrWidth(16), .asyncread("true"), .clearpin("true")) ram_2 (
    .addr(WriteAddr10[15:0]), .we(MemRW10), .oe(mem_ren), .clk(clk), .din(WriteData10), .dout(out_3),
    .clr(rst));
  RAM #(.addrWidth(16), .asyncread("true"), .clearpin("true")) ram_3 (
    .addr(WriteAddr11[15:0]), .we(MemRW11), .oe(mem_ren), .clk(clk), .din(WriteData11), .dout(out_4),
    .clr(rst));

  // Other names for the same wires on the sheet: SH = is_sh; SelOut0[1:0] = WriteAddr[1:0];
  //   WriteData1[7:0] = WriteData[7:0]; WriteData2[7:0] = WriteData[15:8]; WriteData3[7:0] = WriteData[23:16];
  //   WriteData4[7:0] = WriteData[31:24]

  // Notes on the sheet:
  //   INPUTS
  //   lowest 8 bytes
  //   second lowest
  //   OUTPUT
endmodule

module ALU (
  input  [31:0] A,
  input  [31:0] B,
  input  [3:0] ALUSel,
  output [31:0] Result
);

  wire [0:0] slt13, sltiu15;
  wire [31:0] add3, and0, or1, sll14, sra12, srl11, sub4, xor2;

  assign and0 = A & B;  // AND_Gate and_1, 32 bits wide
  Adder #(.width(32)) adder_1 (.a(A), .b(B), .out(add3));  // open: cin, cout
  Shifter #(.shift("lr"), .width(32)) shifter_1 (.in(A), .\dist (B[4:0]), .out(srl11));
  Shifter #(.shift("ar"), .width(32)) shifter_2 (.in(A), .\dist (B[4:0]), .out(sra12));
  Shifter #(.width(32)) shifter_3 (.in(A), .\dist (B[4:0]), .out(sll14));
  assign or1 = A | B;  // OR_Gate or_1, 32 bits wide
  Subtractor #(.width(32)) subtractor_1 (.a(A), .b(B), .out(sub4));  // open: bin, bout
  Comparator #(.width(32)) comparator_1 (.a(A), .b(B), .lt(slt13[0]));  // open: gt, eq
  Comparator #(.mode("unsigned"), .width(32)) comparator_2 (.a(A), .b(B), .lt(sltiu15[0]));  // open: gt, eq
  assign xor2 = A ^ B;  // XOR_Gate xor_1, 32 bits wide
  Multiplexer #(.select(4), .width(32)) multiplexer_1 (
    .in0(and0), .in1(or1), .in2(xor2), .in3(add3), .in4(sub4), .in11(srl11), .in12(sra12),
    .in13({{31{1'b0}}, slt13[0]}), .in14(sll14), .in15({{31{1'b0}}, sltiu15[0]}), .out(Result), .sel(ALUSel));  // open: in5, in6, in7, in8, in9, in10

  // Notes on the sheet:
  //   INPUTS
  //   OUTPUT 
endmodule

module control (
  input  [31:0] Instruction,
  input  BrEq,
  input  BrLT,
  output [2:0] ImmSel,
  output control_en,
  output [1:0] ASel,
  output BSel,
  output [3:0] ALUSel,
  output MemRW,
  output reg_en,
  output [1:0] WBSel,
  output mem_ren,
  output if_sh
);

  wire and_1_out, and_2_out, and_3_out, and_4_out, and_5_out, and_13_out, and_14_out, and_15_out, and_16_out,
       and_17_out, and_18_out, and_19_out, and_20_out, and_21_out, and_22_out, and_23_out, and_24_out,
       and_25_out, and_26_out, BrGT, BrNEq, comparator_1_eq, comparator_2_eq, comparator_3_eq,
       comparator_4_eq, comparator_5_eq, comparator_6_eq, comparator_7_eq, comparator_8_eq, comparator_9_eq,
       comparator_10_eq, comparator_11_eq, comparator_12_eq, comparator_13_eq, comparator_14_eq,
       comparator_15_eq, comparator_16_eq, comparator_17_eq, comparator_18_eq, comparator_19_eq,
       comparator_20_eq, comparator_21_eq, comparator_31_eq, comparator_32_eq, comparator_33_eq,
       comparator_34_eq, comparator_35_eq, comparator_36_eq, comparator_37_eq, comparator_38_eq,
       comparator_39_eq, comparator_40_eq, comparator_41_eq, comparator_42_eq, comparator_43_eq,
       comparator_44_eq, I_type_03, I_type_13, I_type_67, not_3_out, not_4_out, or_1_out, or_2_out, or_3_out,
       or_6_out, or_7_out, or_8_out, or_9_out, or_10_out, R_type, SB_PCSel, SB_type, U_type_17, U_type_37,
       UJ_type;
  wire [1:0] and_30_out, and_31_out, bit_extender_6_out, bit_extender_10_out, multiplexer_23_out,
       multiplexer_24_out;
  wire [2:0] and_7_out, and_8_out, and_9_out, and_10_out, and_11_out, and_32_out, and_33_out, and_34_out,
       and_35_out, and_36_out, bit_extender_1_out, bit_extender_2_out, bit_extender_3_out,
       bit_extender_4_out, bit_extender_5_out, bit_extender_11_out, bit_extender_12_out, bit_extender_13_out,
       bit_extender_14_out, bit_extender_15_out;
  wire [3:0] and_27_out, and_28_out, and_29_out, bit_extender_7_out, bit_extender_8_out, bit_extender_9_out,
       I_ALUSel, multiplexer_1_out, multiplexer_2_out, multiplexer_3_out, multiplexer_4_out,
       multiplexer_5_out, multiplexer_6_out, multiplexer_7_out, multiplexer_8_out, multiplexer_9_out,
       multiplexer_10_out, multiplexer_11_out, multiplexer_12_out, multiplexer_13_out, multiplexer_14_out,
       multiplexer_15_out, multiplexer_16_out, multiplexer_17_out, multiplexer_18_out, multiplexer_19_out,
       multiplexer_20_out, multiplexer_21_out, multiplexer_22_out, R_ALUSel;

  not not_1 (BrNEq, BrEq);
  not not_2 (BrGT, BrLT);
  Comparator #(.width(3)) comparator_1 (.a(Instruction[14:12]), .b(3'b000), .eq(comparator_1_eq));  // open: gt, lt
  Comparator #(.width(3)) comparator_2 (.a(Instruction[14:12]), .b(3'b100), .eq(comparator_2_eq));  // open: gt, lt
  Comparator #(.width(3)) comparator_3 (.a(Instruction[14:12]), .b(3'b110), .eq(comparator_3_eq));  // open: gt, lt
  Comparator #(.width(3)) comparator_4 (.a(Instruction[14:12]), .b(3'b001), .eq(comparator_4_eq));  // open: gt, lt
  Comparator #(.width(3)) comparator_5 (.a(Instruction[14:12]), .b(3'b111), .eq(comparator_5_eq));  // open: gt, lt
  Comparator #(.width(3)) comparator_6 (.a(Instruction[14:12]), .b(3'b000), .eq(comparator_6_eq));  // open: gt, lt
  Comparator #(.width(3)) comparator_7 (.a(Instruction[14:12]), .b(3'b001), .eq(comparator_7_eq));  // open: gt, lt
  Comparator #(.width(3)) comparator_8 (.a(Instruction[14:12]), .b(3'b010), .eq(comparator_8_eq));  // open: gt, lt
  Comparator #(.width(3)) comparator_9 (.a(Instruction[14:12]), .b(3'b100), .eq(comparator_9_eq));  // open: gt, lt
  Comparator #(.width(3)) comparator_10 (.a(Instruction[14:12]), .b(3'b101), .eq(comparator_10_eq));  // open: gt, lt
  Comparator #(.width(3)) comparator_11 (.a(Instruction[14:12]), .b(3'b110), .eq(comparator_11_eq));  // open: gt, lt
  Comparator #(.width(3)) comparator_12 (.a(Instruction[14:12]), .b(3'b111), .eq(comparator_12_eq));  // open: gt, lt
  Comparator #(.width(3)) comparator_13 (.a(Instruction[14:12]), .b(3'b000), .eq(comparator_13_eq));  // open: gt, lt
  Comparator #(.width(3)) comparator_14 (.a(Instruction[14:12]), .b(3'b001), .eq(comparator_14_eq));  // open: gt, lt
  Comparator #(.width(3)) comparator_15 (.a(Instruction[14:12]), .b(3'b011), .eq(comparator_15_eq));  // open: gt, lt
  Comparator #(.width(3)) comparator_16 (.a(Instruction[14:12]), .b(3'b100), .eq(comparator_16_eq));  // open: gt, lt
  Comparator #(.width(3)) comparator_17 (.a(Instruction[14:12]), .b(3'b101), .eq(comparator_17_eq));  // open: gt, lt
  Comparator #(.width(3)) comparator_18 (.a(Instruction[14:12]), .b(3'b110), .eq(comparator_18_eq));  // open: gt, lt
  Comparator #(.width(3)) comparator_19 (.a(Instruction[14:12]), .b(3'b111), .eq(comparator_19_eq));  // open: gt, lt
  Comparator #(.width(3)) comparator_20 (.a(Instruction[14:12]), .b(3'b010), .eq(comparator_20_eq));  // open: gt, lt
  Comparator #(.width(3)) comparator_21 (.a(Instruction[14:12]), .b(3'b001), .eq(comparator_21_eq));  // open: gt, lt
  or or_1 (or_1_out, I_type_03, I_type_13, I_type_67);
  or or_2 (or_2_out, U_type_17, U_type_37);
  and and_1 (and_1_out, BrEq, comparator_1_eq);
  and and_2 (and_2_out, BrLT, comparator_2_eq);
  and and_3 (and_3_out, BrLT, comparator_3_eq);
  and and_4 (and_4_out, BrNEq, comparator_4_eq);
  and and_5 (and_5_out, BrGT, comparator_5_eq);
  Multiplexer #(.width(4)) multiplexer_1 (.in0(4'b0000), .in1(4'b0011), .out(multiplexer_1_out), .sel(comparator_6_eq));
  Multiplexer #(.width(4)) multiplexer_2 (.in0(4'b0000), .in1(4'b1110), .out(multiplexer_2_out), .sel(comparator_7_eq));
  Multiplexer #(.width(4)) multiplexer_3 (.in0(4'b0000), .in1(4'b1101), .out(multiplexer_3_out), .sel(comparator_8_eq));
  Multiplexer #(.width(4)) multiplexer_4 (.in0(4'b0000), .in1(4'b0010), .out(multiplexer_4_out), .sel(comparator_9_eq));
  Multiplexer #(.width(4)) multiplexer_5 (
    .in0(4'b0000), .in1(4'b1011), .out(multiplexer_5_out), .sel(comparator_10_eq));
  Multiplexer #(.width(4)) multiplexer_6 (
    .in0(4'b0000), .in1(4'b0001), .out(multiplexer_6_out), .sel(comparator_11_eq));
  Multiplexer #(.width(4)) multiplexer_7 (
    .in0(4'b0000), .in1(4'b0000), .out(multiplexer_7_out), .sel(comparator_12_eq));
  Multiplexer #(.width(4)) multiplexer_8 (
    .in0(4'b0000), .in1(4'b1111), .out(multiplexer_8_out), .sel(comparator_15_eq));
  and and_6 (if_sh, MemRW, comparator_21_eq);
  Comparator #(.width(7)) comparator_22 (.a(Instruction[6:0]), .b(7'b0110011), .eq(R_type));  // open: gt, lt
  Comparator #(.width(7)) comparator_23 (.a(Instruction[6:0]), .b(7'b0000011), .eq(I_type_03));  // open: gt, lt
  Comparator #(.width(7)) comparator_24 (.a(Instruction[6:0]), .b(7'b0010011), .eq(I_type_13));  // open: gt, lt
  Comparator #(.width(7)) comparator_25 (.a(Instruction[6:0]), .b(7'b0100011), .eq(MemRW));  // open: gt, lt
  Comparator #(.width(7)) comparator_26 (.a(Instruction[6:0]), .b(7'b1100011), .eq(SB_type));  // open: gt, lt
  Comparator #(.width(7)) comparator_27 (.a(Instruction[6:0]), .b(7'b0010111), .eq(U_type_17));  // open: gt, lt
  Comparator #(.width(7)) comparator_28 (.a(Instruction[6:0]), .b(7'b0110111), .eq(U_type_37));  // open: gt, lt
  Comparator #(.width(7)) comparator_29 (.a(Instruction[6:0]), .b(7'b1101111), .eq(UJ_type));  // open: gt, lt
  Comparator #(.width(7)) comparator_30 (.a(Instruction[6:0]), .b(7'b1100111), .eq(I_type_67));  // open: gt, lt
  assign bit_extender_1_out = {{2{or_1_out}}, or_1_out};  // Bit_Extender bit_extender_1
  assign bit_extender_2_out = {{2{MemRW}}, MemRW};  // Bit_Extender bit_extender_2
  assign bit_extender_3_out = {{2{SB_type}}, SB_type};  // Bit_Extender bit_extender_3
  assign bit_extender_4_out = {{2{or_2_out}}, or_2_out};  // Bit_Extender bit_extender_4
  assign bit_extender_5_out = {{2{UJ_type}}, UJ_type};  // Bit_Extender bit_extender_5
  or or_3 (or_3_out, and_1_out, and_2_out, and_3_out, and_4_out, and_5_out);
  assign I_ALUSel = multiplexer_1_out | multiplexer_2_out | multiplexer_3_out | multiplexer_4_out | multiplexer_5_out | multiplexer_6_out | multiplexer_7_out | multiplexer_8_out;  // OR_Gate or_4, 4 bits wide
  assign and_7_out = bit_extender_1_out & 3'b000;  // AND_Gate and_7, 3 bits wide
  assign and_8_out = bit_extender_2_out & 3'b001;  // AND_Gate and_8, 3 bits wide
  assign and_9_out = bit_extender_3_out & 3'b010;  // AND_Gate and_9, 3 bits wide
  assign and_10_out = bit_extender_4_out & 3'b011;  // AND_Gate and_10, 3 bits wide
  assign and_11_out = bit_extender_5_out & 3'b100;  // AND_Gate and_11, 3 bits wide
  Comparator #(.width(7)) comparator_31 (.a(Instruction[31:25]), .b({7{1'b0}}), .eq(comparator_31_eq));  // open: gt, lt
  Comparator #(.width(7)) comparator_32 (
    .a(Instruction[31:25]), .b(7'b0000001), .eq(comparator_32_eq));  // open: gt, lt
  Comparator #(.width(7)) comparator_33 (
    .a(Instruction[31:25]), .b(7'b0100000), .eq(comparator_33_eq));  // open: gt, lt
  Comparator #(.width(7)) comparator_34 (.a(Instruction[31:25]), .b({7{1'b0}}), .eq(comparator_34_eq));  // open: gt, lt
  Comparator #(.width(7)) comparator_35 (
    .a(Instruction[31:25]), .b(7'b0000001), .eq(comparator_35_eq));  // open: gt, lt
  Comparator #(.width(7)) comparator_36 (
    .a(Instruction[31:25]), .b(7'b0000001), .eq(comparator_36_eq));  // open: gt, lt
  Comparator #(.width(7)) comparator_37 (.a(Instruction[31:25]), .b({7{1'b0}}), .eq(comparator_37_eq));  // open: gt, lt
  Comparator #(.width(7)) comparator_38 (
    .a(Instruction[31:25]), .b(7'b0000001), .eq(comparator_38_eq));  // open: gt, lt
  Comparator #(.width(7)) comparator_39 (
    .a(Instruction[31:25]), .b(7'b0100000), .eq(comparator_39_eq));  // open: gt, lt
  Comparator #(.width(7)) comparator_40 (.a(Instruction[31:25]), .b({7{1'b0}}), .eq(comparator_40_eq));  // open: gt, lt
  Comparator #(.width(7)) comparator_41 (.a(Instruction[31:25]), .b({7{1'b0}}), .eq(comparator_41_eq));  // open: gt, lt
  Comparator #(.width(7)) comparator_42 (
    .a(Instruction[31:25]), .b(7'b0000001), .eq(comparator_42_eq));  // open: gt, lt
  Comparator #(.width(7)) comparator_43 (.a(Instruction[31:25]), .b({7{1'b0}}), .eq(comparator_43_eq));  // open: gt, lt
  Comparator #(.width(7)) comparator_44 (.a(Instruction[31:25]), .b({7{1'b0}}), .eq(comparator_44_eq));  // open: gt, lt
  assign ImmSel = and_7_out | and_8_out | and_9_out | and_10_out | and_11_out;  // OR_Gate or_5, 3 bits wide
  and and_12 (SB_PCSel, SB_type, or_3_out);
  and and_13 (and_13_out, comparator_13_eq, comparator_31_eq);
  and and_14 (and_14_out, comparator_13_eq, comparator_32_eq);
  and and_15 (and_15_out, comparator_13_eq, comparator_33_eq);
  and and_16 (and_16_out, comparator_14_eq, comparator_34_eq);
  and and_17 (and_17_out, comparator_14_eq, comparator_35_eq);
  and and_18 (and_18_out, comparator_15_eq, comparator_36_eq);
  and and_19 (and_19_out, comparator_16_eq, comparator_37_eq);
  and and_20 (and_20_out, comparator_16_eq, comparator_38_eq);
  and and_21 (and_21_out, comparator_17_eq, comparator_39_eq);
  and and_22 (and_22_out, comparator_17_eq, comparator_40_eq);
  and and_23 (and_23_out, comparator_18_eq, comparator_41_eq);
  and and_24 (and_24_out, comparator_19_eq, comparator_42_eq);
  and and_25 (and_25_out, comparator_19_eq, comparator_43_eq);
  and and_26 (and_26_out, comparator_20_eq, comparator_44_eq);
  Multiplexer #(.width(4)) multiplexer_9 (.in0(4'b0000), .in1(4'b0011), .out(multiplexer_9_out), .sel(and_13_out));
  Multiplexer #(.width(4)) multiplexer_10 (.in0(4'b0000), .in1(4'b0101), .out(multiplexer_10_out), .sel(and_14_out));
  Multiplexer #(.width(4)) multiplexer_11 (.in0(4'b0000), .in1(4'b0100), .out(multiplexer_11_out), .sel(and_15_out));
  Multiplexer #(.width(4)) multiplexer_12 (.in0(4'b0000), .in1(4'b1110), .out(multiplexer_12_out), .sel(and_16_out));
  Multiplexer #(.width(4)) multiplexer_13 (.in0(4'b0000), .in1(4'b0111), .out(multiplexer_13_out), .sel(and_17_out));
  Multiplexer #(.width(4)) multiplexer_14 (.in0(4'b0000), .in1(4'b0110), .out(multiplexer_14_out), .sel(and_18_out));
  Multiplexer #(.width(4)) multiplexer_15 (.in0(4'b0000), .in1(4'b0010), .out(multiplexer_15_out), .sel(and_19_out));
  Multiplexer #(.width(4)) multiplexer_16 (.in0(4'b0000), .in1(4'b1001), .out(multiplexer_16_out), .sel(and_20_out));
  Multiplexer #(.width(4)) multiplexer_17 (.in0(4'b0000), .in1(4'b1100), .out(multiplexer_17_out), .sel(and_21_out));
  Multiplexer #(.width(4)) multiplexer_18 (.in0(4'b0000), .in1(4'b1011), .out(multiplexer_18_out), .sel(and_22_out));
  Multiplexer #(.width(4)) multiplexer_19 (.in0(4'b0000), .in1(4'b0001), .out(multiplexer_19_out), .sel(and_23_out));
  Multiplexer #(.width(4)) multiplexer_20 (.in0(4'b0000), .in1(4'b1010), .out(multiplexer_20_out), .sel(and_24_out));
  Multiplexer #(.width(4)) multiplexer_21 (.in0(4'b0000), .in1(4'b0000), .out(multiplexer_21_out), .sel(and_25_out));
  Multiplexer #(.width(4)) multiplexer_22 (.in0(4'b0000), .in1(4'b1101), .out(multiplexer_22_out), .sel(and_26_out));
  or or_6 (or_6_out, R_type, U_type_17, U_type_37, I_type_13);
  or or_7 (or_7_out, I_type_13, R_type);
  assign bit_extender_6_out = {{1{or_8_out}}, or_8_out};  // Bit_Extender bit_extender_6
  or or_8 (or_8_out, SB_type, U_type_17, UJ_type);
  Multiplexer #(.width(2)) multiplexer_23 (.in0(2'b10), .in1(2'b01), .out(multiplexer_23_out), .sel(or_6_out));
  or or_9 (or_9_out, I_type_03, I_type_13, I_type_67);
  or or_10 (or_10_out, U_type_17, U_type_37);
  assign bit_extender_7_out = {{3{not_3_out}}, not_3_out};  // Bit_Extender bit_extender_7
  not not_3 (not_3_out, or_7_out);
  assign bit_extender_8_out = {{3{R_type}}, R_type};  // Bit_Extender bit_extender_8
  assign bit_extender_9_out = {{3{I_type_13}}, I_type_13};  // Bit_Extender bit_extender_9
  assign R_ALUSel = multiplexer_9_out | multiplexer_10_out | multiplexer_11_out | multiplexer_12_out | multiplexer_13_out | multiplexer_14_out | multiplexer_16_out | multiplexer_17_out | multiplexer_18_out | multiplexer_19_out | multiplexer_20_out | multiplexer_21_out | multiplexer_22_out;  // OR_Gate or_11, 4 bits wide
  assign bit_extender_10_out = {{1{U_type_37}}, U_type_37};  // Bit_Extender bit_extender_10
  Multiplexer #(.width(2)) multiplexer_24 (
    .in0(multiplexer_23_out), .in1(2'b00), .out(multiplexer_24_out), .sel(I_type_03));
  assign bit_extender_11_out = {{2{or_9_out}}, or_9_out};  // Bit_Extender bit_extender_11
  assign bit_extender_12_out = {{2{MemRW}}, MemRW};  // Bit_Extender bit_extender_12
  assign bit_extender_13_out = {{2{SB_type}}, SB_type};  // Bit_Extender bit_extender_13
  assign bit_extender_14_out = {{2{or_10_out}}, or_10_out};  // Bit_Extender bit_extender_14
  assign bit_extender_15_out = {{2{UJ_type}}, UJ_type};  // Bit_Extender bit_extender_15
  assign and_27_out = 4'b0011 & bit_extender_7_out;  // AND_Gate and_27, 4 bits wide
  assign and_28_out = R_ALUSel & bit_extender_8_out;  // AND_Gate and_28, 4 bits wide
  assign and_29_out = I_ALUSel & bit_extender_9_out;  // AND_Gate and_29, 4 bits wide
  assign and_30_out = bit_extender_6_out & 2'b01;  // AND_Gate and_30, 2 bits wide
  assign and_31_out = bit_extender_10_out & 2'b10;  // AND_Gate and_31, 2 bits wide
  or or_12 (mem_ren, I_type_03, MemRW);
  or or_13 (reg_en, I_type_67, R_type, I_type_03, UJ_type, I_type_13, U_type_17, U_type_37);
  Multiplexer #(.width(2)) multiplexer_25 (.in0(multiplexer_24_out), .in1(2'b11), .out(WBSel), .sel(not_4_out));
  not not_4 (not_4_out, reg_en);
  assign and_32_out = bit_extender_11_out & 3'b000;  // AND_Gate and_32, 3 bits wide
  assign and_33_out = bit_extender_12_out & 3'b001;  // AND_Gate and_33, 3 bits wide
  assign and_34_out = bit_extender_13_out & 3'b010;  // AND_Gate and_34, 3 bits wide
  assign and_35_out = bit_extender_14_out & 3'b011;  // AND_Gate and_35, 3 bits wide
  assign and_36_out = bit_extender_15_out & 3'b100;  // AND_Gate and_36, 3 bits wide
  assign ALUSel = and_27_out | and_28_out | and_29_out;  // OR_Gate or_14, 4 bits wide
  not not_5 (BSel, R_type);
  assign ASel = and_30_out | and_31_out;  // OR_Gate or_15, 2 bits wide
  or or_16 (control_en, SB_PCSel, UJ_type, I_type_67);
  assign ImmSel = and_32_out | and_33_out | and_34_out | and_35_out | and_36_out;  // OR_Gate or_17, 3 bits wide

  // Other names for the same wires on the sheet: inst[31:0] = Instruction; Opcode[6:0] = Instruction[6:0];
  //   funct3[2:0] = Instruction[14:12]; funct7[6:0] = Instruction[31:25]; mem_wen = MemRW; S_type = MemRW; SH = if_sh;
  //   wb_en = reg_en

  // Notes on the sheet:
  //   ADD
endmodule

module imm_gen (
  input  [31:0] Inst,
  input  [2:0] Imm_sel,
  output [31:0] Imm
);

  wire [31:0] bit_extender_1_out, bit_extender_2_out, bit_extender_3_out, bit_extender_4_out,
       bit_extender_5_out;

  assign bit_extender_1_out = {{20{Inst[31]}}, Inst[31:20]};  // Bit_Extender bit_extender_1
  assign bit_extender_2_out = {{20{Inst[31]}}, {Inst[31:25], Inst[11:7]}};  // Bit_Extender bit_extender_2
  assign bit_extender_3_out = {{19{Inst[31]}}, {Inst[31], Inst[7], Inst[30:25], Inst[11:8], 1'b0}};  // Bit_Extender bit_extender_3
  Bit_Extender #(.in_width(32), .out_width(32)) bit_extender_4 (
    .in({Inst[31:12], {12{1'b0}}}), .out(bit_extender_4_out));
  assign bit_extender_5_out = {{11{Inst[31]}}, {Inst[31], Inst[19:12], Inst[20], Inst[30:21], 1'b0}};  // Bit_Extender bit_extender_5
  Multiplexer #(.select(3), .width(32)) multiplexer_1 (
    .in0(bit_extender_1_out), .in1(bit_extender_2_out), .in2(bit_extender_3_out), .in3(bit_extender_4_out),
    .in4(bit_extender_5_out), .out(Imm), .sel(Imm_sel));  // open: in5, in6, in7

  // Notes on the sheet:
  //   Take away opcode 0-6
  //   I-type
  //   S-type
  //   B-type
  //   U-type
  //   J-type
  //   Imm [11:0]
  //   Imm [4:0] Imm[11:5]
  //   Imm[31:12]
  //   Imm [4:1] Imm [11] Imm[10:5] Imm[12]
  //   Imm[19:12] Imm[11] Imm[10:1] Imm[20]
endmodule
