// Logisim project proj_2_1_top.circ as structural Verilog: 7 circuits, main circuit testbench
module TOP (
  input  clk,
  input  rst,
  input  [31:0] inst,
  output [31:0] inst_addr,
  output mem_wen,
  output [31:0] mem_din,
  output [31:0] mem_dout,
  output [31:0] mem_addr,
  output control_en,
  output [31:0] control_pc,
  output wb_en,
  output [4:0] wb_addr,
  output [31:0] wb_data
);

  wire BrEq, BrLT, BrUn, BSel, comparator_1_lt, comparator_2_lt, control_1_memrw, control_1_pcsel,
       control_1_reg_en, mem_ren;
  wire [0:0] and_1_out;
  wire [1:0] and_2_out, and_3_out, ASel, bit_extender_1_out, bit_extender_2_out, or_1_out, WBSel;
  wire [2:0] Imm_sel;
  wire [3:0] ALUSel;
  wire [31:0] adder_1_out, alu_result, and_4_out, bit_extender_3_out, bit_extender_4_out, bit_extender_5_out,
       bit_extender_6_out, bit_extender_7_out, bit_extender_8_out, dmem_1_readdata, Gen_Imm, instr_addr,
       multiplexer_2_out, multiplexer_3_out, multiplexer_4_out, multiplexer_6_out, multiplexer_7_out,
       multiplexer_8_out, multiplexer_9_out, PC_q, r1, r2, register_1_q;

  Comparator #(.width(32)) comparator_1 (.a(r1), .b(r2), .eq(BrEq), .lt(comparator_1_lt));  // open: gt
  Comparator #(.mode("unsigned"), .width(32)) comparator_2 (.a(r1), .b(r2), .lt(comparator_2_lt));  // open: gt, eq
  Multiplexer multiplexer_1 (.in0(comparator_1_lt), .in1(comparator_2_lt), .out(BrLT), .sel(BrUn));
  Multiplexer #(.select(2), .width(32)) multiplexer_2 (
    .in0(r1), .in1(instr_addr), .in2({32{1'b0}}), .out(multiplexer_2_out), .sel(ASel));  // open: in3
  Multiplexer #(.width(32)) multiplexer_3 (.in0(r2), .in1(Gen_Imm), .out(multiplexer_3_out), .sel(BSel));
  Multiplexer #(.width(32)) multiplexer_4 (
    .in0(adder_1_out), .in1(alu_result), .out(multiplexer_4_out), .sel(control_en));
  imm_gen imm_gen_1 (.Inst(inst), .Imm_sel(Imm_sel), .Imm(Gen_Imm));
  Register #(.width(32)) PC (.D(multiplexer_4_out), .en(1'b1), .clk(clk), .Q(PC_q));  // open: clr
  Register #(.width(32)) register_1 (.D(PC_q), .en(1'b1), .clk(clk), .Q(register_1_q));  // open: clr
  regfile regfile_1 (
    .Read_Register_1_rs1(inst[19:15]), .Read_Register_2_rs2(inst[24:20]), .Write_Register_rd(wb_addr),
    .Write_Data(wb_data), .Write_Enable(wb_en), .Clock(clk), .RST(rst), .Read_Data_1(r1), .Read_Data_2(r2));  // open: ra, sp, t0, t1, t2, s0, s1, a0
  Adder #(.width(32)) adder_1 (.a(32'h4), .b(PC_q), .out(adder_1_out));  // open: cin, cout
  ALU alu_1 (.A(multiplexer_2_out), .B(multiplexer_3_out), .ALUSel(ALUSel), .Result(alu_result));
  and and_1 (and_1_out[0], 1'b0, register_1_q[0]);
  Multiplexer #(.width(32)) multiplexer_5 (
    .in0({register_1_q[31:1], and_1_out[0]}), .in1({32{1'b0}}), .out(inst_addr), .sel(rst));
  assign bit_extender_1_out = {{1{mem_ren}}, mem_ren};  // Bit_Extender bit_extender_1
  assign bit_extender_2_out = {{1{wb_en}}, wb_en};  // Bit_Extender bit_extender_2
  assign and_2_out = bit_extender_1_out & 2'b10;  // AND_Gate and_2, 2 bits wide
  assign and_3_out = bit_extender_2_out & 2'b01;  // AND_Gate and_3, 2 bits wide
  DMEM dmem_1 (
    .mem_ren(mem_ren), .WriteAddr(alu_result), .WriteData(mem_din), .MemRW(mem_wen), .clk(clk), .rst(rst),
    .ReadData(dmem_1_readdata));
  control control_1 (
    .Instruction(inst), .BrEq(BrEq), .BrLT(BrLT), .ImmSel(Imm_sel), .PCSel(control_1_pcsel), .ASel(ASel),
    .BSel(BSel), .ALUSel(ALUSel), .MemRW(control_1_memrw), .reg_en(control_1_reg_en), .WBSel(WBSel),
    .mem_addr(mem_ren));
  assign or_1_out = and_2_out | and_3_out;  // OR_Gate or_1, 2 bits wide
  assign bit_extender_3_out = {{31{mem_wen}}, mem_wen};  // Bit_Extender bit_extender_3
  assign bit_extender_4_out = {{24{dmem_1_readdata[7]}}, dmem_1_readdata[7:0]};  // Bit_Extender bit_extender_4
  assign bit_extender_5_out = {{16{dmem_1_readdata[15]}}, dmem_1_readdata[15:0]};  // Bit_Extender bit_extender_5
  Bit_Extender #(.in_width(32), .out_width(32)) bit_extender_6 (.in(dmem_1_readdata), .out(bit_extender_6_out));
  assign bit_extender_7_out = {{24{dmem_1_readdata[7]}}, dmem_1_readdata[7:0]};  // Bit_Extender bit_extender_7
  assign bit_extender_8_out = {{16{dmem_1_readdata[15]}}, dmem_1_readdata[15:0]};  // Bit_Extender bit_extender_8
  assign and_4_out = bit_extender_3_out & r2;  // AND_Gate and_4, 32 bits wide
  Multiplexer #(.select(3), .width(32)) multiplexer_6 (
    .in0(bit_extender_4_out), .in1(bit_extender_5_out), .in2(bit_extender_6_out), .in3(bit_extender_7_out),
    .in4(bit_extender_8_out), .out(multiplexer_6_out), .sel(inst[14:12]));  // open: in5, in6, in7
  Multiplexer #(.select(2), .width(32)) multiplexer_7 (
    .in0({32{1'b0}}), .in1(alu_result), .in2({32{1'b0}}), .in3(mem_dout), .out(multiplexer_7_out),
    .sel(or_1_out));
  Multiplexer #(.width(32)) multiplexer_8 (
    .in0({32{1'b0}}), .in1(alu_result), .out(multiplexer_8_out), .sel(control_en));
  Multiplexer #(.width(32)) multiplexer_9 (.in0({32{1'b0}}), .in1(alu_result), .out(multiplexer_9_out), .sel(mem_ren));
  Multiplexer multiplexer_10 (.in0(control_1_pcsel), .in1(1'b0), .out(control_en), .sel(rst));
  Multiplexer #(.width(32)) multiplexer_11 (.in0(and_4_out), .in1({32{1'b0}}), .out(mem_din), .sel(rst));
  Multiplexer #(.width(5)) multiplexer_12 (.in0(inst[11:7]), .in1({5{1'b0}}), .out(wb_addr), .sel(rst));
  Multiplexer #(.width(32)) multiplexer_13 (.in0(multiplexer_8_out), .in1({32{1'b0}}), .out(control_pc), .sel(rst));
  Multiplexer multiplexer_14 (.in0(control_1_memrw), .in1(1'b0), .out(mem_wen), .sel(rst));
  Multiplexer multiplexer_15 (.in0(control_1_reg_en), .in1(1'b0), .out(wb_en), .sel(rst));
  Multiplexer #(.width(32)) multiplexer_16 (.in0(multiplexer_6_out), .in1({32{1'b0}}), .out(mem_dout), .sel(rst));
  Multiplexer #(.width(32)) multiplexer_17 (.in0(multiplexer_7_out), .in1({32{1'b0}}), .out(wb_data), .sel(rst));
  Multiplexer #(.width(32)) multiplexer_18 (.in0(multiplexer_9_out), .in1({32{1'b0}}), .out(mem_addr), .sel(rst));

  // Other names for the same wires on the sheet: Opcode[6:0] = inst[6:0]; funct3[2:0] = inst[14:12];
  //   write_rs1_addr[4:0] = inst[19:15]; write_rs2_addr[4:0] = inst[24:20]; funct7[6:0] = inst[31:25]

  // Notes on the sheet:
  //   B type comparator
  //   unsigned comparator
  //   DON'T TOUCH!
  //   pcsel=1,alu result will be suitable for auipc
  //   enable writing value to pc
  //   lw/lh
endmodule

module testbench (
  input  rst,
  output [5:0] out_2,
  output out_3,
  output halt,
  output [31:0] out_5,
  output [31:0] mem_dout,
  output [31:0] mem_addr,
  output out_8,
  output [31:0] out_9,
  output out_10,
  output [4:0] out_11,
  output [31:0] out_12
);

  wire and_1_out, carry, clk, not_1_out, not_2_out, por_1_out, rst_t;
  wire [31:0] inst, inst_addr;

  not not_1 (not_1_out, inst[2]);
  not not_2 (not_2_out, inst[3]);
  POR por_1 (.out(por_1_out));
  TOP top_1 (
    .clk(clk), .rst(rst_t), .inst(inst), .inst_addr(inst_addr), .mem_wen(out_3), .mem_din(out_5),
    .mem_dout(mem_dout), .mem_addr(mem_addr), .control_en(out_8), .control_pc(out_9), .wb_en(out_10),
    .wb_addr(out_11), .wb_data(out_12));
  Clock clock_1 (.out(clk));
  or or_1 (rst_t, rst, por_1_out);
  and and_1 (and_1_out, inst[0], inst[1], not_1_out, not_2_out, inst[4], inst[5], inst[6]);
  or or_2 (halt, and_1_out, carry);
  Counter #(.max('h3f), .width(6)) counter_1 (
    .clr(rst_t), .up(1'b1), .count(1'b1), .clk(clk), .carry(carry), .Q(out_2));  // open: load, D
  // ROM #(.line("quad"), .misaligned("true")) inst_mem: pin names not known; wires that end beside it: inst_addr[7:0], inst[7:0], inst[15:8], inst[23:16], inst[31:24]
  // Probe on inst

  // Other names for the same wires on the sheet: control_en = out_8; control_pc[31:0] = out_9; mem_din[31:0] = out_5;
  //   mem_wen = out_3; wb_addr[4:0] = out_11; wb_data[31:0] = out_12; wb_en = out_10

  // Notes on the sheet:
  //   DON'T TOUCH!
  //   contents of inst_mem (hex, n*v repeats v):
  //   13 1 20 0 23 23 20 0 3 22 41
  //   you can write any instruction in
endmodule

module regfile (
  input  [4:0] Read_Register_1_rs1,
  input  [4:0] Read_Register_2_rs2,
  input  [4:0] Write_Register_rd,
  input  [31:0] Write_Data,
  input  Write_Enable,
  input  Clock,
  input  RST,
  output [31:0] ra,
  output [31:0] sp,
  output [31:0] t0,
  output [31:0] t1,
  output [31:0] t2,
  output [31:0] s0,
  output [31:0] s1,
  output [31:0] a0,
  output [31:0] Read_Data_1,
  output [31:0] Read_Data_2
);

  wire demultiplexer_1_out1, demultiplexer_1_out2, demultiplexer_1_out3, demultiplexer_1_out4,
       demultiplexer_1_out5, demultiplexer_1_out6, demultiplexer_1_out7, demultiplexer_1_out8,
       demultiplexer_1_out9, demultiplexer_1_out10, demultiplexer_1_out11, demultiplexer_1_out12,
       demultiplexer_1_out13, demultiplexer_1_out14, demultiplexer_1_out15, demultiplexer_1_out16,
       demultiplexer_1_out17, demultiplexer_1_out18, demultiplexer_1_out19, demultiplexer_1_out20,
       demultiplexer_1_out21, demultiplexer_1_out22, demultiplexer_1_out23, demultiplexer_1_out24,
       demultiplexer_1_out25, demultiplexer_1_out26, demultiplexer_1_out27, demultiplexer_1_out28,
       demultiplexer_1_out29, demultiplexer_1_out30, demultiplexer_1_out31;
  wire [31:0] a1, a2, a3, a4, a5, a6, a7, gp, s2, s3, s4, s5, s6, s7, s8, s9, s10, s11, t3, t4, t5, t6, tp;

  Demultiplexer #(.select(5)) demultiplexer_1 (
    .out1(demultiplexer_1_out1), .out2(demultiplexer_1_out2), .out3(demultiplexer_1_out3),
    .out4(demultiplexer_1_out4), .out5(demultiplexer_1_out5), .out6(demultiplexer_1_out6),
    .out7(demultiplexer_1_out7), .out8(demultiplexer_1_out8), .out9(demultiplexer_1_out9),
    .out10(demultiplexer_1_out10), .out11(demultiplexer_1_out11), .out12(demultiplexer_1_out12),
    .out13(demultiplexer_1_out13), .out14(demultiplexer_1_out14), .out15(demultiplexer_1_out15),
    .out16(demultiplexer_1_out16), .out17(demultiplexer_1_out17), .out18(demultiplexer_1_out18),
    .out19(demultiplexer_1_out19), .out20(demultiplexer_1_out20), .out21(demultiplexer_1_out21),
    .out22(demultiplexer_1_out22), .out23(demultiplexer_1_out23), .out24(demultiplexer_1_out24),
    .out25(demultiplexer_1_out25), .out26(demultiplexer_1_out26), .out27(demultiplexer_1_out27),
    .out28(demultiplexer_1_out28), .out29(demultiplexer_1_out29), .out30(demultiplexer_1_out30),
    .out31(demultiplexer_1_out31), .in(Write_Enable), .sel(Write_Register_rd));  // open: out0
  Register #(.width(32)) register_1 (.D(Write_Data), .en(demultiplexer_1_out1), .clk(Clock), .Q(ra), .clr(RST));
  Register #(.width(32)) register_2 (.D(Write_Data), .en(demultiplexer_1_out2), .clk(Clock), .Q(sp), .clr(RST));
  Register #(.width(32)) register_3 (.D(Write_Data), .en(demultiplexer_1_out3), .clk(Clock), .Q(gp), .clr(RST));
  Register #(.width(32)) register_4 (.D(Write_Data), .en(demultiplexer_1_out4), .clk(Clock), .Q(tp), .clr(RST));
  Register #(.width(32)) register_5 (.D(Write_Data), .en(demultiplexer_1_out5), .clk(Clock), .Q(t0), .clr(RST));
  Register #(.width(32)) register_6 (.D(Write_Data), .en(demultiplexer_1_out6), .clk(Clock), .Q(t1), .clr(RST));
  Register #(.width(32)) register_7 (.D(Write_Data), .en(demultiplexer_1_out7), .clk(Clock), .Q(t2), .clr(RST));
  Register #(.width(32)) register_8 (.D(Write_Data), .en(demultiplexer_1_out8), .clk(Clock), .Q(s0), .clr(RST));
  Register #(.width(32)) register_9 (.D(Write_Data), .en(demultiplexer_1_out9), .clk(Clock), .Q(s1), .clr(RST));
  Register #(.width(32)) register_10 (.D(Write_Data), .en(demultiplexer_1_out10), .clk(Clock), .Q(a0), .clr(RST));
  Register #(.width(32)) register_11 (.D(Write_Data), .en(demultiplexer_1_out11), .clk(Clock), .Q(a1), .clr(RST));
  Register #(.width(32)) register_12 (.D(Write_Data), .en(demultiplexer_1_out12), .clk(Clock), .Q(a2), .clr(RST));
  Register #(.width(32)) register_13 (.D(Write_Data), .en(demultiplexer_1_out13), .clk(Clock), .Q(a3), .clr(RST));
  Register #(.width(32)) register_14 (.D(Write_Data), .en(demultiplexer_1_out14), .clk(Clock), .Q(a4), .clr(RST));
  Register #(.width(32)) register_15 (.D(Write_Data), .en(demultiplexer_1_out15), .clk(Clock), .Q(a5), .clr(RST));
  Register #(.width(32)) register_16 (.D(Write_Data), .en(demultiplexer_1_out16), .clk(Clock), .Q(a6), .clr(RST));
  Register #(.width(32)) register_17 (.D(Write_Data), .en(demultiplexer_1_out17), .clk(Clock), .Q(a7), .clr(RST));
  Register #(.width(32)) register_18 (.D(Write_Data), .en(demultiplexer_1_out18), .clk(Clock), .Q(s2), .clr(RST));
  Register #(.width(32)) register_19 (.D(Write_Data), .en(demultiplexer_1_out19), .clk(Clock), .Q(s3), .clr(RST));
  Register #(.width(32)) register_20 (.D(Write_Data), .en(demultiplexer_1_out20), .clk(Clock), .Q(s4), .clr(RST));
  Register #(.width(32)) register_21 (.D(Write_Data), .en(demultiplexer_1_out21), .clk(Clock), .Q(s5), .clr(RST));
  Register #(.width(32)) register_22 (.D(Write_Data), .en(demultiplexer_1_out22), .clk(Clock), .Q(s6), .clr(RST));
  Register #(.width(32)) register_23 (.D(Write_Data), .en(demultiplexer_1_out23), .clk(Clock), .Q(s7), .clr(RST));
  Register #(.width(32)) register_24 (.D(Write_Data), .en(demultiplexer_1_out24), .clk(Clock), .Q(s8), .clr(RST));
  Register #(.width(32)) register_25 (.D(Write_Data), .en(demultiplexer_1_out25), .clk(Clock), .Q(s9), .clr(RST));
  Register #(.width(32)) register_26 (.D(Write_Data), .en(demultiplexer_1_out26), .clk(Clock), .Q(s10), .clr(RST));
  Register #(.width(32)) register_27 (.D(Write_Data), .en(demultiplexer_1_out27), .clk(Clock), .Q(s11), .clr(RST));
  Register #(.width(32)) register_28 (.D(Write_Data), .en(demultiplexer_1_out28), .clk(Clock), .Q(t3), .clr(RST));
  Register #(.width(32)) register_29 (.D(Write_Data), .en(demultiplexer_1_out29), .clk(Clock), .Q(t4), .clr(RST));
  Register #(.width(32)) register_30 (.D(Write_Data), .en(demultiplexer_1_out30), .clk(Clock), .Q(t5), .clr(RST));
  Register #(.width(32)) register_31 (.D(Write_Data), .en(demultiplexer_1_out31), .clk(Clock), .Q(t6), .clr(RST));
  Multiplexer #(.select(5), .width(32)) multiplexer_1 (
    .in0({32{1'b0}}), .in1(ra), .in2(sp), .in3(gp), .in4(tp), .in5(t0), .in6(t1), .in7(t2), .in8(s0),
    .in9(s1), .in10(a0), .in11(a1), .in12(a2), .in13(a3), .in14(a4), .in15(a5), .in16(a6), .in17(a7),
    .in18(s2), .in19(s3), .in20(s4), .in21(s5), .in22(s6), .in23(s7), .in24(s8), .in25(s9), .in26(s10),
    .in27(s11), .in28(t3), .in29(t4), .in30(t5), .in31(t6), .out(Read_Data_1), .sel(Read_Register_1_rs1));
  Multiplexer #(.select(5), .width(32)) multiplexer_2 (
    .in0({32{1'b0}}), .in1(ra), .in2(sp), .in3(gp), .in4(tp), .in5(t0), .in6(t1), .in7(t2), .in8(s0),
    .in9(s1), .in10(a0), .in11(a1), .in12(a2), .in13(a3), .in14(a4), .in15(a5), .in16(a6), .in17(a7),
    .in18(s2), .in19(s3), .in20(s4), .in21(s5), .in22(s6), .in23(s7), .in24(s8), .in25(s9), .in26(s10),
    .in27(s11), .in28(t3), .in29(t4), .in30(t5), .in31(t6), .out(Read_Data_2), .sel(Read_Register_2_rs2));

  // Other names for the same wires on the sheet: clk = Clock; read_data1[31:0] = Read_Data_1;
  //   read_data2[31:0] = Read_Data_2; read_reg1[4:0] = Read_Register_1_rs1; read_reg2[4:0] = Read_Register_2_rs2;
  //   write_en = Write_Enable; write_reg[4:0] = Write_Register_rd
endmodule

module DMEM (
  input  mem_ren,
  input  [31:0] WriteAddr,
  input  [31:0] WriteData,
  input  MemRW,
  input  clk,
  input  rst,
  output [31:0] ReadData
);

  wire [31:0] ram_1_dout;

  RAM #(.addrWidth(16), .asyncread("true"), .clearpin("true"), .dataWidth(32)) ram_1 (
    .addr(WriteAddr[15:0]), .we(MemRW), .oe(mem_ren), .clk(clk), .din(WriteData), .dout(ram_1_dout), .clr(rst));
  Multiplexer #(.width(32)) multiplexer_1 (.in0({32{1'b0}}), .in1(ram_1_dout), .out(ReadData), .sel(mem_ren));

  // Notes on the sheet:
  //   INPUTS
  //   OUTPUT
endmodule

module ALU (
  input  [31:0] A,
  input  [31:0] B,
  input  [3:0] ALUSel,
  output [31:0] Result
);

  wire [0:0] slt13;
  wire [6:0] cnto15;
  wire [31:0] add3, and0, or1, sll14, sra12, srl11, sub4, xor2;

  assign and0 = A & B;  // AND_Gate and_1, 32 bits wide
  Adder #(.width(32)) adder_1 (.a(A), .b(B), .out(add3));  // open: cin, cout
  Shifter #(.shift("lr"), .width(32)) shifter_1 (.in(A), .\dist (B[4:0]), .out(srl11));
  Shifter #(.shift("ar"), .width(32)) shifter_2 (.in(A), .\dist (B[4:0]), .out(sra12));
  Shifter #(.width(32)) shifter_3 (.in(A), .\dist (B[4:0]), .out(sll14));
  assign or1 = A | B;  // OR_Gate or_1, 32 bits wide
  Subtractor #(.width(32)) subtractor_1 (.a(A), .b(B), .out(sub4));  // open: bin, bout
  Comparator #(.width(32)) comparator_1 (.a(A), .b(B), .lt(slt13[0]));  // open: gt, eq
  assign xor2 = A ^ B;  // XOR_Gate xor_1, 32 bits wide
  BitAdder #(.width(32)) bitadder_1 (.in0(A), .in1(B), .out(cnto15));
  Multiplexer #(.select(4), .width(32)) multiplexer_1 (
    .in0(and0), .in1(or1), .in2(xor2), .in3(add3), .in4(sub4), .in11(srl11), .in12(sra12),
    .in13({{31{1'b0}}, slt13[0]}), .in14(sll14), .out(Result), .sel(ALUSel));  // open: in5, in6, in7, in8, in9, in10, in15

  // Notes on the sheet:
  //   INPUTS
  //   OUTPUT 
endmodule

module control (
  input  [31:0] Instruction,
  input  BrEq,
  input  BrLT,
  output [2:0] ImmSel,
  output PCSel,
  output [1:0] ASel,
  output BSel,
  output [3:0] ALUSel,
  output MemRW,
  output reg_en,
  output [1:0] WBSel,
  output mem_addr
);

  wire and_6_out, and_7_out, and_8_out, and_9_out, and_10_out, and_12_out, and_13_out, and_14_out,
       and_15_out, and_16_out, and_17_out, and_18_out, and_19_out, and_20_out, and_21_out, and_22_out,
       and_23_out, and_24_out, and_25_out, BrGT, BrNEq, comparator_1_eq, comparator_2_eq, comparator_3_eq,
       comparator_4_eq, comparator_5_eq, comparator_6_eq, comparator_7_eq, comparator_8_eq, comparator_9_eq,
       comparator_10_eq, comparator_11_eq, comparator_12_eq, comparator_13_eq, comparator_14_eq,
       comparator_15_eq, comparator_16_eq, comparator_17_eq, comparator_18_eq, comparator_19_eq,
       comparator_20_eq, comparator_30_eq, comparator_31_eq, comparator_32_eq, comparator_33_eq,
       comparator_34_eq, comparator_35_eq, comparator_36_eq, comparator_37_eq, comparator_38_eq,
       comparator_39_eq, comparator_40_eq, comparator_41_eq, comparator_42_eq, comparator_43_eq, I_type_03,
       I_type_13, I_type_67, not_3_out, or_1_out, or_2_out, or_4_out, or_6_out, or_7_out, or_8_out, or_9_out,
       or_10_out, or_12_out, R_type, SB_PCSel, SB_type, U_type_17, U_type_37, UJ_type;
  wire [1:0] and_29_out, and_30_out, bit_extender_6_out, bit_extender_10_out, multiplexer_8_out,
       multiplexer_24_out;
  wire [2:0] and_1_out, and_2_out, and_3_out, and_4_out, and_5_out, and_31_out, and_32_out, and_33_out,
       and_34_out, and_35_out, bit_extender_1_out, bit_extender_2_out, bit_extender_3_out,
       bit_extender_4_out, bit_extender_5_out, bit_extender_11_out, bit_extender_12_out, bit_extender_13_out,
       bit_extender_14_out, bit_extender_15_out;
  wire [3:0] and_26_out, and_27_out, and_28_out, bit_extender_7_out, bit_extender_8_out, bit_extender_9_out,
       I_ALUSel, multiplexer_1_out, multiplexer_2_out, multiplexer_3_out, multiplexer_4_out,
       multiplexer_5_out, multiplexer_6_out, multiplexer_7_out, multiplexer_10_out, multiplexer_11_out,
       multiplexer_12_out, multiplexer_13_out, multiplexer_14_out, multiplexer_15_out, multiplexer_16_out,
       multiplexer_17_out, multiplexer_18_out, multiplexer_19_out, multiplexer_20_out, multiplexer_21_out,
       multiplexer_22_out, multiplexer_23_out, R_ALUSel;

  not not_1 (BrNEq, BrEq);
  not not_2 (BrGT, BrLT);
  Comparator #(.width(3)) comparator_1 (.a(Instruction[14:12]), .b(3'b000), .eq(comparator_1_eq));  // open: gt, lt
  Comparator #(.width(3)) comparator_2 (.a(Instruction[14:12]), .b(3'b100), .eq(comparator_2_eq));  // open: gt, lt
  Comparator #(.width(3)) comparator_3 (.a(Instruction[14:12]), .b(3'b110), .eq(comparator_3_eq));  // open: gt, lt
  Comparator #(.width(3)) comparator_4 (.a(Instruction[14:12]), .b(3'b001), .eq(comparator_4_eq));  // open: gt, lt
  Comparator #(.width(3)) comparator_5 (.a(Instruction[14:12]), .b(3'b111), .eq(comparator_5_eq));  // open: gt, lt
  Comparator #(.width(3)) comparator_6 (.a(Instruction[14:12]), .b(3'b000), .eq(comparator_6_eq));  // open: gt, lt
  Comparator #(.width(3)) comparator_7 (.a(Instruction[14:12]), .b(3'b001), .eq(comparator_7_eq));  // open: gt, lt
  Comparator #(.width(3)) comparator_8 (.a(Instruction[14:12]), .b(3'b010), .eq(comparator_8_eq));  // open: gt, lt
  Comparator #(.width(3)) comparator_9 (.a(Instruction[14:12]), .b(3'b100), .eq(comparator_9_eq));  // open: gt, lt
  Comparator #(.width(3)) comparator_10 (.a(Instruction[14:12]), .b(3'b101), .eq(comparator_10_eq));  // open: gt, lt
  Comparator #(.width(3)) comparator_11 (.a(Instruction[14:12]), .b(3'b110), .eq(comparator_11_eq));  // open: gt, lt
  Comparator #(.width(3)) comparator_12 (.a(Instruction[14:12]), .b(3'b111), .eq(comparator_12_eq));  // open: gt, lt
  Comparator #(.width(3)) comparator_13 (.a(Instruction[14:12]), .b(3'b000), .eq(comparator_13_eq));  // open: gt, lt
  Comparator #(.width(3)) comparator_14 (.a(Instruction[14:12]), .b(3'b001), .eq(comparator_14_eq));  // open: gt, lt
  Comparator #(.width(3)) comparator_15 (.a(Instruction[14:12]), .b(3'b011), .eq(comparator_15_eq));  // open: gt, lt
  Comparator #(.width(3)) comparator_16 (.a(Instruction[14:12]), .b(3'b100), .eq(comparator_16_eq));  // open: gt, lt
  Comparator #(.width(3)) comparator_17 (.a(Instruction[14:12]), .b(3'b101), .eq(comparator_17_eq));  // open: gt, lt
  Comparator #(.width(3)) comparator_18 (.a(Instruction[14:12]), .b(3'b110), .eq(comparator_18_eq));  // open: gt, lt
  Comparator #(.width(3)) comparator_19 (.a(Instruction[14:12]), .b(3'b111), .eq(comparator_19_eq));  // open: gt, lt
  Comparator #(.width(3)) comparator_20 (.a(Instruction[14:12]), .b(3'b010), .eq(comparator_20_eq));  // open: gt, lt
  or or_1 (or_1_out, I_type_03, I_type_13, I_type_67);
  or or_2 (or_2_out, U_type_17, U_type_37);
  assign bit_extender_1_out = {{2{or_1_out}}, or_1_out};  // Bit_Extender bit_extender_1
  assign and_1_out = bit_extender_1_out & 3'b000;  // AND_Gate and_1, 3 bits wide
  assign bit_extender_2_out = {{2{MemRW}}, MemRW};  // Bit_Extender bit_extender_2
  assign and_2_out = bit_extender_2_out & 3'b001;  // AND_Gate and_2, 3 bits wide
  assign bit_extender_3_out = {{2{SB_type}}, SB_type};  // Bit_Extender bit_extender_3
  assign and_3_out = bit_extender_3_out & 3'b010;  // AND_Gate and_3, 3 bits wide
  assign bit_extender_4_out = {{2{or_2_out}}, or_2_out};  // Bit_Extender bit_extender_4
  assign and_4_out = bit_extender_4_out & 3'b011;  // AND_Gate and_4, 3 bits wide
  assign bit_extender_5_out = {{2{UJ_type}}, UJ_type};  // Bit_Extender bit_extender_5
  assign and_5_out = bit_extender_5_out & 3'b100;  // AND_Gate and_5, 3 bits wide
  assign ImmSel = and_1_out | and_2_out | and_3_out | and_4_out | and_5_out;  // OR_Gate or_3, 3 bits wide
  and and_6 (and_6_out, BrEq, comparator_1_eq);
  and and_7 (and_7_out, BrLT, comparator_2_eq);
  and and_8 (and_8_out, BrLT, comparator_3_eq);
  and and_9 (and_9_out, BrNEq, comparator_4_eq);
  and and_10 (and_10_out, BrGT, comparator_5_eq);
  Multiplexer #(.width(4)) multiplexer_1 (.in0(4'b0000), .in1(4'b0011), .out(multiplexer_1_out), .sel(comparator_6_eq));
  Multiplexer #(.width(4)) multiplexer_2 (.in0(4'b0000), .in1(4'b1110), .out(multiplexer_2_out), .sel(comparator_7_eq));
  Multiplexer #(.width(4)) multiplexer_3 (.in0(4'b0000), .in1(4'b1101), .out(multiplexer_3_out), .sel(comparator_8_eq));
  Multiplexer #(.width(4)) multiplexer_4 (.in0(4'b0000), .in1(4'b0010), .out(multiplexer_4_out), .sel(comparator_9_eq));
  Multiplexer #(.width(4)) multiplexer_5 (
    .in0(4'b0000), .in1(4'b1011), .out(multiplexer_5_out), .sel(comparator_10_eq));
  Multiplexer #(.width(4)) multiplexer_6 (
    .in0(4'b0000), .in1(4'b0001), .out(multiplexer_6_out), .sel(comparator_11_eq));
  Multiplexer #(.width(4)) multiplexer_7 (
    .in0(4'b0000), .in1(4'b0000), .out(multiplexer_7_out), .sel(comparator_12_eq));
  Comparator #(.width(7)) comparator_21 (.a(Instruction[6:0]), .b(7'b0110011), .eq(R_type));  // open: gt, lt
  Comparator #(.width(7)) comparator_22 (.a(Instruction[6:0]), .b(7'b0000011), .eq(I_type_03));  // open: gt, lt
  Comparator #(.width(7)) comparator_23 (.a(Instruction[6:0]), .b(7'b0010011), .eq(I_type_13));  // open: gt, lt
  Comparator #(.width(7)) comparator_24 (.a(Instruction[6:0]), .b(7'b0100011), .eq(MemRW));  // open: gt, lt
  Comparator #(.width(7)) comparator_25 (.a(Instruction[6:0]), .b(7'b1100011), .eq(SB_type));  // open: gt, lt
  Comparator #(.width(7)) comparator_26 (.a(Instruction[6:0]), .b(7'b0010111), .eq(U_type_17));  // open: gt, lt
  Comparator #(.width(7)) comparator_27 (.a(Instruction[6:0]), .b(7'b0110111), .eq(U_type_37));  // open: gt, lt
  Comparator #(.width(7)) comparator_28 (.a(Instruction[6:0]), .b(7'b1101111), .eq(UJ_type));  // open: gt, lt
  Comparator #(.width(7)) comparator_29 (.a(Instruction[6:0]), .b(7'b1100111), .eq(I_type_67));  // open: gt, lt
  or or_4 (or_4_out, and_6_out, and_7_out, and_8_out, and_9_out, and_10_out);
  assign I_ALUSel = multiplexer_1_out | multiplexer_2_out | multiplexer_3_out | multiplexer_4_out | multiplexer_5_out | multiplexer_6_out | multiplexer_7_out;  // OR_Gate or_5, 4 bits wide
  or or_6 (or_6_out, R_type, I_type_13, U_type_17, U_type_37);
  Comparator #(.width(7)) comparator_30 (.a(Instruction[31:25]), .b({7{1'b0}}), .eq(comparator_30_eq));  // open: gt, lt
  Comparator #(.width(7)) comparator_31 (
    .a(Instruction[31:25]), .b(7'b0000001), .eq(comparator_31_eq));  // open: gt, lt
  Comparator #(.width(7)) comparator_32 (
    .a(Instruction[31:25]), .b(7'b0100000), .eq(comparator_32_eq));  // open: gt, lt
  Comparator #(.width(7)) comparator_33 (.a(Instruction[31:25]), .b({7{1'b0}}), .eq(comparator_33_eq));  // open: gt, lt
  Comparator #(.width(7)) comparator_34 (
    .a(Instruction[31:25]), .b(7'b0000001), .eq(comparator_34_eq));  // open: gt, lt
  Comparator #(.width(7)) comparator_35 (
    .a(Instruction[31:25]), .b(7'b0000001), .eq(comparator_35_eq));  // open: gt, lt
  Comparator #(.width(7)) comparator_36 (.a(Instruction[31:25]), .b({7{1'b0}}), .eq(comparator_36_eq));  // open: gt, lt
  Comparator #(.width(7)) comparator_37 (
    .a(Instruction[31:25]), .b(7'b0000001), .eq(comparator_37_eq));  // open: gt, lt
  Comparator #(.width(7)) comparator_38 (
    .a(Instruction[31:25]), .b(7'b0000001), .eq(comparator_38_eq));  // open: gt, lt
  Comparator #(.width(7)) comparator_39 (.a(Instruction[31:25]), .b({7{1'b0}}), .eq(comparator_39_eq));  // open: gt, lt
  Comparator #(.width(7)) comparator_40 (.a(Instruction[31:25]), .b({7{1'b0}}), .eq(comparator_40_eq));  // open: gt, lt
  Comparator #(.width(7)) comparator_41 (
    .a(Instruction[31:25]), .b(7'b0000001), .eq(comparator_41_eq));  // open: gt, lt
  Comparator #(.width(7)) comparator_42 (.a(Instruction[31:25]), .b({7{1'b0}}), .eq(comparator_42_eq));  // open: gt, lt
  Comparator #(.width(7)) comparator_43 (.a(Instruction[31:25]), .b({7{1'b0}}), .eq(comparator_43_eq));  // open: gt, lt
  Multiplexer #(.width(2)) multiplexer_8 (.in0(2'b10), .in1(2'b01), .out(multiplexer_8_out), .sel(or_6_out));
  and and_11 (SB_PCSel, SB_type, or_4_out);
  and and_12 (and_12_out, comparator_13_eq, comparator_30_eq);
  and and_13 (and_13_out, comparator_13_eq, comparator_31_eq);
  and and_14 (and_14_out, comparator_13_eq, comparator_32_eq);
  and and_15 (and_15_out, comparator_14_eq, comparator_33_eq);
  and and_16 (and_16_out, comparator_14_eq, comparator_34_eq);
  and and_17 (and_17_out, comparator_15_eq, comparator_35_eq);
  and and_18 (and_18_out, comparator_16_eq, comparator_36_eq);
  and and_19 (and_19_out, comparator_16_eq, comparator_37_eq);
  and and_20 (and_20_out, comparator_17_eq, comparator_38_eq);
  and and_21 (and_21_out, comparator_17_eq, comparator_39_eq);
  and and_22 (and_22_out, comparator_18_eq, comparator_40_eq);
  and and_23 (and_23_out, comparator_19_eq, comparator_41_eq);
  and and_24 (and_24_out, comparator_19_eq, comparator_42_eq);
  and and_25 (and_25_out, comparator_20_eq, comparator_43_eq);
  Multiplexer #(.width(2)) multiplexer_9 (.in0(multiplexer_8_out), .in1(2'b00), .out(WBSel), .sel(I_type_03));
  Multiplexer #(.width(4)) multiplexer_10 (.in0(4'b0000), .in1(4'b0011), .out(multiplexer_10_out), .sel(and_12_out));
  Multiplexer #(.width(4)) multiplexer_11 (.in0(4'b0000), .in1(4'b0101), .out(multiplexer_11_out), .sel(and_13_out));
  Multiplexer #(.width(4)) multiplexer_12 (.in0(4'b0000), .in1(4'b0100), .out(multiplexer_12_out), .sel(and_14_out));
  Multiplexer #(.width(4)) multiplexer_13 (.in0(4'b0000), .in1(4'b1110), .out(multiplexer_13_out), .sel(and_15_out));
  Multiplexer #(.width(4)) multiplexer_14 (.in0(4'b0000), .in1(4'b0111), .out(multiplexer_14_out), .sel(and_16_out));
  Multiplexer #(.width(4)) multiplexer_15 (.in0(4'b0000), .in1(4'b0110), .out(multiplexer_15_out), .sel(and_17_out));
  Multiplexer #(.width(4)) multiplexer_16 (.in0(4'b0000), .in1(4'b0010), .out(multiplexer_16_out), .sel(and_18_out));
  Multiplexer #(.width(4)) multiplexer_17 (.in0(4'b0000), .in1(4'b1001), .out(multiplexer_17_out), .sel(and_19_out));
  Multiplexer #(.width(4)) multiplexer_18 (.in0(4'b0000), .in1(4'b1000), .out(multiplexer_18_out), .sel(and_20_out));
  Multiplexer #(.width(4)) multiplexer_19 (.in0(4'b0000), .in1(4'b1011), .out(multiplexer_19_out), .sel(and_21_out));
  Multiplexer #(.width(4)) multiplexer_20 (.in0(4'b0000), .in1(4'b0001), .out(multiplexer_20_out), .sel(and_22_out));
  Multiplexer #(.width(4)) multiplexer_21 (.in0(4'b0000), .in1(4'b1010), .out(multiplexer_21_out), .sel(and_23_out));
  Multiplexer #(.width(4)) multiplexer_22 (.in0(4'b0000), .in1(4'b0000), .out(multiplexer_22_out), .sel(and_24_out));
  Multiplexer #(.width(4)) multiplexer_23 (.in0(4'b0000), .in1(4'b1101), .out(multiplexer_23_out), .sel(and_25_out));
  or or_7 (or_7_out, I_type_13, R_type);
  assign bit_extender_6_out = {{1{or_8_out}}, or_8_out};  // Bit_Extender bit_extender_6
  or or_8 (or_8_out, SB_type, U_type_17, UJ_type);
  or or_9 (or_9_out, I_type_03, I_type_13, I_type_67);
  or or_10 (or_10_out, U_type_17, U_type_37);
  assign bit_extender_7_out = {{3{not_3_out}}, not_3_out};  // Bit_Extender bit_extender_7
  not not_3 (not_3_out, or_7_out);
  assign bit_extender_8_out = {{3{R_type}}, R_type};  // Bit_Extender bit_extender_8
  assign bit_extender_9_out = {{3{I_type_13}}, I_type_13};  // Bit_Extender bit_extender_9
  assign R_ALUSel = multiplexer_10_out | multiplexer_11_out | multiplexer_12_out | multiplexer_13_out | multiplexer_14_out | multiplexer_15_out | multiplexer_17_out | multiplexer_18_out | multiplexer_19_out | multiplexer_20_out | multiplexer_21_out | multiplexer_22_out | multiplexer_23_out;  // OR_Gate or_11, 4 bits wide
  assign bit_extender_10_out = {{1{U_type_37}}, U_type_37};  // Bit_Extender bit_extender_10
  or or_12 (or_12_out, R_type, I_type_13);
  assign bit_extender_11_out = {{2{or_9_out}}, or_9_out};  // Bit_Extender bit_extender_11
  assign bit_extender_12_out = {{2{MemRW}}, MemRW};  // Bit_Extender bit_extender_12
  assign bit_extender_13_out = {{2{SB_type}}, SB_type};  // Bit_Extender bit_extender_13
  assign bit_extender_14_out = {{2{or_10_out}}, or_10_out};  // Bit_Extender bit_extender_14
  assign bit_extender_15_out = {{2{UJ_type}}, UJ_type};  // Bit_Extender bit_extender_15
  assign and_26_out = 4'b0011 & bit_extender_7_out;  // AND_Gate and_26, 4 bits wide
  assign and_27_out = R_ALUSel & bit_extender_8_out;  // AND_Gate and_27, 4 bits wide
  assign and_28_out = I_ALUSel & bit_extender_9_out;  // AND_Gate and_28, 4 bits wide
  assign and_29_out = bit_extender_6_out & 2'b01;  // AND_Gate and_29, 2 bits wide
  assign and_30_out = bit_extender_10_out & 2'b10;  // AND_Gate and_30, 2 bits wide
  or or_13 (mem_addr, I_type_03, MemRW);
  or or_14 (reg_en, R_type, I_type_03, I_type_13, U_type_17, U_type_37);
  Multiplexer #(.width(2)) multiplexer_24 (.in0(2'b10), .in1(2'b01), .out(multiplexer_24_out), .sel(or_12_out));
  assign and_31_out = bit_extender_11_out & 3'b000;  // AND_Gate and_31, 3 bits wide
  assign and_32_out = bit_extender_12_out & 3'b001;  // AND_Gate and_32, 3 bits wide
  assign and_33_out = bit_extender_13_out & 3'b010;  // AND_Gate and_33, 3 bits wide
  assign and_34_out = bit_extender_14_out & 3'b011;  // AND_Gate and_34, 3 bits wide
  assign and_35_out = bit_extender_15_out & 3'b100;  // AND_Gate and_35, 3 bits wide
  assign ALUSel = and_26_out | and_27_out | and_28_out;  // OR_Gate or_15, 4 bits wide
  not not_4 (BSel, R_type);
  assign ASel = and_29_out | and_30_out;  // OR_Gate or_16, 2 bits wide
  or or_17 (PCSel, SB_PCSel, UJ_type, I_type_67);
  Multiplexer #(.width(2)) multiplexer_25 (.in0(multiplexer_24_out), .in1(2'b00), .out(WBSel), .sel(I_type_03));
  assign ImmSel = and_31_out | and_32_out | and_33_out | and_34_out | and_35_out;  // OR_Gate or_18, 3 bits wide

  // Other names for the same wires on the sheet: control_en = PCSel; inst[31:0] = Instruction;
  //   Opcode[6:0] = Instruction[6:0]; funct3[2:0] = Instruction[14:12]; funct7[6:0] = Instruction[31:25];
  //   mem_ren = mem_addr; mem_wen = MemRW; S_type = MemRW; wb_en = reg_en

  // Notes on the sheet:
  //   ADD
endmodule

module imm_gen (
  input  [31:0] Inst,
  input  [2:0] Imm_sel,
  output [31:0] Imm
);

  wire [31:0] bit_extender_1_out, bit_extender_2_out, bit_extender_3_out, bit_extender_4_out,
       bit_extender_5_out;

  assign bit_extender_1_out = {{20{Inst[31]}}, Inst[31:20]};  // Bit_Extender bit_extender_1
  assign bit_extender_2_out = {{20{Inst[31]}}, {Inst[31:25], Inst[11:7]}};  // Bit_Extender bit_extender_2
  assign bit_extender_3_out = {{19{Inst[31]}}, {Inst[31], Inst[7], Inst[30:25], Inst[11:8], 1'b0}};  // Bit_Extender bit_extender_3
  Bit_Extender #(.in_width(32), .out_width(32)) bit_extender_4 (
    .in({Inst[31:12], {12{1'b0}}}), .out(bit_extender_4_out));
  assign bit_extender_5_out = {{11{Inst[31]}}, {Inst[31], Inst[19:12], Inst[20], Inst[30:21], 1'b0}};  // Bit_Extender bit_extender_5
  Multiplexer #(.select(3), .width(32)) multiplexer_1 (
    .in0(bit_extender_1_out), .in1(bit_extender_2_out), .in2(bit_extender_3_out), .in3(bit_extender_4_out),
    .in4(bit_extender_5_out), .out(Imm), .sel(Imm_sel));  // open: in5, in6, in7

  // Notes on the sheet:
  //   Take away opcode 0-6
  //   I-type
  //   S-type
  //   B-type
  //   U-type
  //   J-type
  //   Imm [11:0]
  //   Imm [4:0] Imm[11:5]
  //   Imm[31:12]
  //   Imm [4:1] Imm [11] Imm[10:5] Imm[12]
  //   Imm[19:12] Imm[11] Imm[10:1] Imm[20]
endmodule
