// Logisim project proj_2_2_top.circ as structural Verilog: 12 circuits, main circuit TOP
module TOP (
  input  clk,
  input  rst,
  input  [31:0] inst,
  output [31:0] current_pc_if,
  output mem_wen_mem,
  output [31:0] mem_din_mem,
  output [31:0] mem_dout_mem,
  output [31:0] mem_addr_mem,
  output control_en_mem,
  output [31:0] control_pc_mem,
  output wb_en_wb,
  output [4:0] wb_addr_wb,
  output [31:0] wb_data_wb
);

  wire and_1_out, and_2_out, comparator_1_eq, comparator_2_eq, comparator_3_eq, comparator_4_eq,
       comparator_5_eq, comparator_6_eq, comparator_7_eq, comparator_8_eq, comparator_9_eq, comparator_10_eq,
       comparator_11_eq, comparator_12_eq, ex_stage_1_control_en_mem, ex_stage_1_is_sh_mem, ex_stage_1_islw,
       ex_stage_1_mem_ren_mem, ex_stage_1_mem_wen_mem, ex_stage_1_wb_en_mem, id_stage_1_bsel_ex,
       id_stage_1_control_en_ex, id_stage_1_is_i03, id_stage_1_is_sb, id_stage_1_is_sh_ex,
       id_stage_1_mem_ren_ex, id_stage_1_mem_wen_ex, id_stage_1_rea1, id_stage_1_rea2, id_stage_1_wb_en_ex,
       if_stage_1_bsel, if_stage_1_control_en_mem, if_stage_1_if_sh, if_stage_1_is_i03, if_stage_1_is_sb,
       if_stage_1_mem_ren, if_stage_1_memrw, if_stage_1_read_1, if_stage_1_read_2, if_stage_1_wb_en_wb,
       ifwrite_pre_1, ifwrite_pre_2, is_I03, mem_stage_1_wb_en_wb, not_1_out, not_2_out, not_3_out,
       not_4_out, not_5_out, not_6_out, not_7_out, not_8_out, or_1_out, or_2_out, read_1, read_2,
       register_1_q, register_3_q, register_5_q, register_6_q, register_8_q, register_9_q, register_14_q,
       register_15_q, register_17_q, register_18_q, register_24_q, register_26_q, register_28_q,
       register_30_q, register_32_q, register_33_q, register_38_q, register_39_q, register_42_q,
       register_43_q, register_45_q, register_47_q, register_53_q;
  wire [1:0] ex_stage_1_wbsel_mem, id_stage_1_asel_ex, id_stage_1_wb_sel_ex, if_stage_1_asel,
       if_stage_1_wbsel, mem_stage_1_wbsel_wb, register_2_q, register_7_q, register_25_q, register_29_q,
       register_44_q, register_60_q;
  wire [2:0] Selread_data1, Selread_data2;
  wire [3:0] id_stage_1_alusel_ex, if_stage_1_alusel, register_4_q, register_27_q;
  wire [4:0] ex_stage_1_wb_addr_mem, id_stage_1_rd, if_stage_1_rd, if_stage_1_rs1, if_stage_1_rs2,
       mem_stage_1_wb_addr_wb, rd_pre_1, rd_pre_2, register_10_q, register_11_q, register_13_q,
       register_34_q, rs_1, rs_2;
  wire [31:0] ex_stage_1_alu_result_mem, ex_stage_1_control_pc_mem, ex_stage_1_current_pc_mem,
       ex_stage_1_inst, ex_stage_1_mem_addr_mem, ex_stage_1_mem_din_mem, id_stage_1_control_pc_ex,
       id_stage_1_imm_ex, id_stage_1_inst, id_stage_1_r1, id_stage_1_r2, if_stage_1_current_pc_id,
       if_stage_1_imm, if_stage_1_inst_id, mem_stage_1_alu_result, mem_stage_1_current_pc,
       mem_stage_1_mem_sign_dout, multiplexer_1_out, multiplexer_2_out, register_12_q, register_16_q,
       register_21_q, register_22_q, register_23_q, register_31_q, register_37_q, register_40_q,
       register_41_q, register_49_q, register_50_q, register_51_q, register_52_q, register_54_q,
       register_56_q, register_57_q, register_61_q;

  IF_stage if_stage_1 (
    .current_pc(current_pc_if), .control_pc_mem(control_pc_mem), .Instruction(inst), .RST(rst), .clk(clk),
    .control_en(control_en_mem), .current_pc_id(if_stage_1_current_pc_id),
    .control_en_mem(if_stage_1_control_en_mem), .ASel(if_stage_1_asel), .BSel(if_stage_1_bsel),
    .ALUSel(if_stage_1_alusel), .MemRW(if_stage_1_memrw), .wb_en_wb(if_stage_1_wb_en_wb),
    .WBSel(if_stage_1_wbsel), .mem_ren(if_stage_1_mem_ren), .if_sh(if_stage_1_if_sh), .rs2(if_stage_1_rs2),
    .rs1(if_stage_1_rs1), .imm(if_stage_1_imm), .rd(if_stage_1_rd), .read_1(if_stage_1_read_1),
    .read_2(if_stage_1_read_2), .inst_id(if_stage_1_inst_id), .is_Sb(if_stage_1_is_sb),
    .is_I03(if_stage_1_is_i03));
  Register #(.width(32)) PC (.D(if_stage_1_current_pc_id), .clk(clk), .Q(current_pc_if), .clr(rst));  // open: en
  Register #(.width(1)) register_1 (
    .D(if_stage_1_control_en_mem), .clk(clk), .Q(register_1_q), .clr(or_1_out));  // open: en
  Register #(.width(2)) register_2 (.D(if_stage_1_asel), .clk(clk), .Q(register_2_q), .clr(or_1_out));  // open: en
  Register #(.width(1)) register_3 (.D(if_stage_1_bsel), .clk(clk), .Q(register_3_q), .clr(or_1_out));  // open: en
  Register #(.width(4)) register_4 (.D(if_stage_1_alusel), .clk(clk), .Q(register_4_q), .clr(or_1_out));  // open: en
  Register #(.width(1)) register_5 (.D(if_stage_1_memrw), .clk(clk), .Q(register_5_q), .clr(or_1_out));  // open: en
  Register #(.width(1)) register_6 (.D(if_stage_1_wb_en_wb), .clk(clk), .Q(register_6_q), .clr(or_1_out));  // open: en
  Register #(.width(2)) register_7 (.D(if_stage_1_wbsel), .clk(clk), .Q(register_7_q), .clr(or_1_out));  // open: en
  Register #(.width(1)) register_8 (.D(if_stage_1_mem_ren), .clk(clk), .Q(register_8_q), .clr(or_1_out));  // open: en
  Register #(.width(1)) register_9 (.D(if_stage_1_if_sh), .clk(clk), .Q(register_9_q), .clr(or_1_out));  // open: en
  Register #(.width(5)) register_10 (.D(if_stage_1_rs2), .clk(clk), .Q(register_10_q), .clr(or_1_out));  // open: en
  Register #(.width(5)) register_11 (.D(if_stage_1_rs1), .clk(clk), .Q(register_11_q), .clr(or_1_out));  // open: en
  Register #(.width(32)) register_12 (.D(if_stage_1_imm), .clk(clk), .Q(register_12_q), .clr(or_1_out));  // open: en
  Register #(.width(5)) register_13 (.D(if_stage_1_rd), .clk(clk), .Q(register_13_q), .clr(or_1_out));  // open: en
  Register #(.width(1)) register_14 (.D(if_stage_1_read_1), .clk(clk), .Q(register_14_q), .clr(or_1_out));  // open: en
  Register #(.width(1)) register_15 (.D(if_stage_1_read_2), .clk(clk), .Q(register_15_q), .clr(or_1_out));  // open: en
  Register #(.width(32)) register_16 (
    .D(if_stage_1_inst_id), .clk(clk), .Q(register_16_q), .clr(or_1_out));  // open: en
  Register #(.width(1)) register_17 (.D(if_stage_1_is_sb), .clk(clk), .Q(register_17_q), .clr(or_1_out));  // open: en
  Register #(.width(1)) register_18 (.D(if_stage_1_is_i03), .clk(clk), .Q(register_18_q), .clr(or_1_out));  // open: en
  or or_1 (or_1_out, rst, control_en_mem);
  ID_stage id_stage_1 (
    .current_pc_id(current_pc_if), .control_en_id(register_1_q), .ASel(register_2_q), .BSel(register_3_q),
    .ALUSel(register_4_q), .MemRW(register_5_q), .wb_en_id(register_6_q), .WBSel(register_7_q),
    .mem_ren(register_8_q), .if_sh(register_9_q), .rs2(register_10_q), .rs1(register_11_q),
    .imm(register_12_q), .rd_ex(register_13_q), .wb_data_wb(wb_data_wb), .RST(rst), .clk(clk),
    .rd_wb(wb_addr_wb), .wb_en_wb(wb_en_wb), .re1(register_14_q), .re2(register_15_q),
    .Instruction(register_16_q), .issb(register_17_q), .lw(register_18_q),
    .control_pc_ex(id_stage_1_control_pc_ex), .r1(id_stage_1_r1), .r2(id_stage_1_r2),
    .control_en_ex(id_stage_1_control_en_ex), .ASel_ex(id_stage_1_asel_ex), .BSel_ex(id_stage_1_bsel_ex),
    .ALUSel_ex(id_stage_1_alusel_ex), .mem_wen_ex(id_stage_1_mem_wen_ex), .wb_sel_ex(id_stage_1_wb_sel_ex),
    .is_sh_ex(id_stage_1_is_sh_ex), .imm_ex(id_stage_1_imm_ex), .wb_en_ex(id_stage_1_wb_en_ex),
    .mem_ren_ex(id_stage_1_mem_ren_ex), .rd(id_stage_1_rd), .rea1(id_stage_1_rea1), .rea2(id_stage_1_rea2),
    .inst(id_stage_1_inst), .is_sb(id_stage_1_is_sb), .is_i03(id_stage_1_is_i03));
  not not_1 (not_1_out, is_I03);
  Register #(.width(5)) register_19 (.D(register_11_q), .clk(clk), .Q(rs_1), .clr(or_2_out));  // open: en
  Register #(.width(5)) register_20 (.D(register_10_q), .clk(clk), .Q(rs_2), .clr(or_2_out));  // open: en
  Register #(.width(32)) register_21 (
    .D(id_stage_1_control_pc_ex), .clk(clk), .Q(register_21_q), .clr(rst));  // open: en
  Register #(.width(32)) register_22 (.D(id_stage_1_r1), .clk(clk), .Q(register_22_q), .clr(or_2_out));  // open: en
  Register #(.width(32)) register_23 (.D(id_stage_1_r2), .clk(clk), .Q(register_23_q), .clr(or_2_out));  // open: en
  Register #(.width(1)) register_24 (
    .D(id_stage_1_control_en_ex), .clk(clk), .Q(register_24_q), .clr(or_2_out));  // open: en
  Register #(.width(2)) register_25 (.D(id_stage_1_asel_ex), .clk(clk), .Q(register_25_q), .clr(or_2_out));  // open: en
  Register #(.width(1)) register_26 (.D(id_stage_1_bsel_ex), .clk(clk), .Q(register_26_q), .clr(or_2_out));  // open: en
  Register #(.width(4)) register_27 (
    .D(id_stage_1_alusel_ex), .clk(clk), .Q(register_27_q), .clr(or_2_out));  // open: en
  Register #(.width(1)) register_28 (
    .D(id_stage_1_mem_wen_ex), .clk(clk), .Q(register_28_q), .clr(or_2_out));  // open: en
  Register #(.width(2)) register_29 (
    .D(id_stage_1_wb_sel_ex), .clk(clk), .Q(register_29_q), .clr(or_2_out));  // open: en
  Register #(.width(1)) register_30 (
    .D(id_stage_1_is_sh_ex), .clk(clk), .Q(register_30_q), .clr(or_2_out));  // open: en
  Register #(.width(32)) register_31 (.D(id_stage_1_imm_ex), .clk(clk), .Q(register_31_q), .clr(or_2_out));  // open: en
  Register #(.width(1)) register_32 (
    .D(id_stage_1_wb_en_ex), .clk(clk), .Q(register_32_q), .clr(or_2_out));  // open: en
  Register #(.width(1)) register_33 (
    .D(id_stage_1_mem_ren_ex), .clk(clk), .Q(register_33_q), .clr(or_2_out));  // open: en
  Register #(.width(5)) register_34 (.D(id_stage_1_rd), .clk(clk), .Q(register_34_q), .clr(or_2_out));  // open: en
  Register #(.width(1)) register_35 (.D(id_stage_1_rea1), .clk(clk), .Q(read_1), .clr(or_2_out));  // open: en
  Register #(.width(1)) register_36 (.D(id_stage_1_rea2), .clk(clk), .Q(read_2), .clr(or_2_out));  // open: en
  Register #(.width(32)) register_37 (.D(id_stage_1_inst), .clk(clk), .Q(register_37_q), .clr(or_2_out));  // open: en
  Register #(.width(1)) register_38 (.D(id_stage_1_is_sb), .clk(clk), .Q(register_38_q), .clr(or_2_out));  // open: en
  Register #(.width(1)) register_39 (.D(id_stage_1_is_i03), .clk(clk), .Q(register_39_q), .clr(or_2_out));  // open: en
  not not_2 (not_2_out, is_I03);
  or or_2 (or_2_out, rst, control_en_mem);
  and and_1 (and_1_out, ifwrite_pre_2, not_1_out);
  and and_2 (and_2_out, ifwrite_pre_2, not_2_out);
  Comparator #(.width(5)) comparator_1 (.a(rd_pre_1), .b(rs_1), .eq(comparator_1_eq));  // open: gt, lt
  Comparator #(.width(5)) comparator_2 (.a(rd_pre_2), .b(rs_2), .eq(comparator_2_eq));  // open: gt, lt
  Comparator #(.width(5)) comparator_3 (.a(rd_pre_1), .b(rs_2), .eq(comparator_3_eq));  // open: gt, lt
  Comparator #(.width(5)) comparator_4 (.a({5{1'b0}}), .b(rs_2), .eq(comparator_4_eq));  // open: gt, lt
  Comparator #(.width(5)) comparator_5 (.a(rd_pre_2), .b(rs_2), .eq(comparator_5_eq));  // open: gt, lt
  Comparator #(.width(5)) comparator_6 (.a({5{1'b0}}), .b(rs_2), .eq(comparator_6_eq));  // open: gt, lt
  Comparator #(.width(5)) comparator_7 (.a(rd_pre_2), .b(rs_1), .eq(comparator_7_eq));  // open: gt, lt
  Comparator #(.width(5)) comparator_8 (.a({5{1'b0}}), .b(rs_1), .eq(comparator_8_eq));  // open: gt, lt
  not not_3 (not_3_out, comparator_9_eq);
  Comparator #(.width(5)) comparator_9 (.a({5{1'b0}}), .b(rs_1), .eq(comparator_9_eq));  // open: gt, lt
  Comparator #(.width(5)) comparator_10 (.a(rd_pre_2), .b(rs_1), .eq(comparator_10_eq));  // open: gt, lt
  Comparator #(.width(5)) comparator_11 (.a({5{1'b0}}), .b(rs_1), .eq(comparator_11_eq));  // open: gt, lt
  not not_4 (not_4_out, comparator_12_eq);
  Comparator #(.width(5)) comparator_12 (.a({5{1'b0}}), .b(rs_2), .eq(comparator_12_eq));  // open: gt, lt
  not not_5 (not_5_out, comparator_4_eq);
  not not_6 (not_6_out, comparator_6_eq);
  Multiplexer #(.select(3), .width(32)) multiplexer_1 (
    .in0(register_22_q), .in1(register_57_q), .in2(register_41_q), .in3(register_22_q), .in4(register_54_q),
    .in5(register_22_q), .in6(register_41_q), .in7(register_22_q), .out(multiplexer_1_out),
    .sel(Selread_data1));
  not not_7 (not_7_out, comparator_8_eq);
  not not_8 (not_8_out, comparator_11_eq);
  Multiplexer #(.select(3), .width(32)) multiplexer_2 (
    .in0(register_23_q), .in1(register_57_q), .in2(register_41_q), .in3(register_23_q), .in4(register_54_q),
    .in5(register_23_q), .in6(register_41_q), .in7(register_23_q), .out(multiplexer_2_out),
    .sel(Selread_data2));
  and and_3 (Selread_data2[1], ifwrite_pre_1, read_2, comparator_3_eq, not_5_out);
  and and_4 (Selread_data2[2], and_1_out, read_2, comparator_5_eq, not_6_out);
  EX_stage ex_stage_1 (
    .current_pc_ex(register_21_q), .r1(multiplexer_1_out), .r2(multiplexer_2_out),
    .control_en_ex(register_24_q), .ASel_ex(register_25_q), .BSel_ex(register_26_q),
    .ALUSel_ex(register_27_q), .mem_wen_ex(register_28_q), .wb_sel_ex(register_29_q),
    .is_sh_ex(register_30_q), .imm_ex(register_31_q), .wb_en_ex(register_32_q), .mem_ren_ex(register_33_q),
    .rd_ex(register_34_q), .Instruction(register_37_q), .is_sb(register_38_q), .is_lw(register_39_q),
    .current_pc_mem(ex_stage_1_current_pc_mem), .alu_result_mem(ex_stage_1_alu_result_mem),
    .control_en_mem(ex_stage_1_control_en_mem), .mem_wen_mem(ex_stage_1_mem_wen_mem),
    .WBSel_mem(ex_stage_1_wbsel_mem), .is_sh_mem(ex_stage_1_is_sh_mem), .wb_en_mem(ex_stage_1_wb_en_mem),
    .mem_ren_mem(ex_stage_1_mem_ren_mem), .wb_addr_mem(ex_stage_1_wb_addr_mem),
    .mem_din_mem(ex_stage_1_mem_din_mem), .control_pc_mem(ex_stage_1_control_pc_mem),
    .mem_addr_mem(ex_stage_1_mem_addr_mem), .inst(ex_stage_1_inst), .islw(ex_stage_1_islw));
  and and_5 (Selread_data1[0], is_I03, read_1, comparator_7_eq, not_7_out);
  and and_6 (Selread_data1[1], ifwrite_pre_1, read_1, comparator_1_eq, not_3_out);
  and and_7 (Selread_data1[2], and_2_out, read_1, comparator_10_eq, not_8_out);
  and and_8 (Selread_data2[0], is_I03, read_2, comparator_2_eq, not_4_out);
  Register #(.width(32)) register_40 (
    .D(ex_stage_1_current_pc_mem), .clk(clk), .Q(register_40_q), .clr(rst));  // open: en
  Register #(.width(32)) register_41 (
    .D(ex_stage_1_alu_result_mem), .clk(clk), .Q(register_41_q), .clr(rst));  // open: en
  Register #(.width(1)) register_42 (
    .D(ex_stage_1_control_en_mem), .clk(clk), .Q(register_42_q), .clr(rst));  // open: en
  Register #(.width(1)) register_43 (.D(ex_stage_1_mem_wen_mem), .clk(clk), .Q(register_43_q), .clr(rst));  // open: en
  Register #(.width(2)) register_44 (.D(ex_stage_1_wbsel_mem), .clk(clk), .Q(register_44_q), .clr(rst));  // open: en
  Register #(.width(1)) register_45 (.D(ex_stage_1_is_sh_mem), .clk(clk), .Q(register_45_q), .clr(rst));  // open: en
  Register #(.width(1)) register_46 (.D(ex_stage_1_wb_en_mem), .clk(clk), .Q(ifwrite_pre_1), .clr(rst));  // open: en
  Register #(.width(1)) register_47 (.D(ex_stage_1_mem_ren_mem), .clk(clk), .Q(register_47_q), .clr(rst));  // open: en
  Register #(.width(5)) register_48 (.D(ex_stage_1_wb_addr_mem), .clk(clk), .Q(rd_pre_1), .clr(rst));  // open: en
  Register #(.width(32)) register_49 (.D(ex_stage_1_mem_din_mem), .clk(clk), .Q(register_49_q), .clr(rst));  // open: en
  Register #(.width(32)) register_50 (
    .D(ex_stage_1_control_pc_mem), .clk(clk), .Q(register_50_q), .clr(rst));  // open: en
  Register #(.width(32)) register_51 (
    .D(ex_stage_1_mem_addr_mem), .clk(clk), .Q(register_51_q), .clr(rst));  // open: en
  Register #(.width(32)) register_52 (.D(ex_stage_1_inst), .clk(clk), .Q(register_52_q), .clr(rst));  // open: en
  Register #(.width(1)) register_53 (.D(ex_stage_1_islw), .clk(clk), .Q(register_53_q), .clr(rst));  // open: en
  Register #(.width(32)) register_54 (.D(register_41_q), .clk(clk), .Q(register_54_q), .clr(rst));  // open: en
  Register #(.width(1)) register_55 (.D(register_53_q), .clk(clk), .Q(is_I03), .clr(rst));  // open: en
  MEM_stage mem_stage_1 (
    .current_pc_mem(register_40_q), .alu_result_mem(register_41_q), .control_en_mem(register_42_q),
    .mem_wen_mem(register_43_q), .WBSel_mem(register_44_q), .is_sh_mem(register_45_q),
    .wb_en_mem(ifwrite_pre_1), .mem_ren_mem(register_47_q), .wb_addr_mem(rd_pre_1),
    .mem_din_mem(register_49_q), .control_pc_mem(register_50_q), .mem_addr_mem(register_51_q), .RST(rst),
    .clk(clk), .inst(register_52_q), .current_pc(mem_stage_1_current_pc), .mem_dout(mem_dout_mem),
    .mem_sign_dout(mem_stage_1_mem_sign_dout), .wb_en_wb(mem_stage_1_wb_en_wb),
    .wb_addr_wb(mem_stage_1_wb_addr_wb), .mem_wen(mem_wen_mem), .mem_din(mem_din_mem),
    .control_pc(control_pc_mem), .control_en(control_en_mem), .mem_addr(mem_addr_mem),
    .WBSel_wb(mem_stage_1_wbsel_wb), .alu_result(mem_stage_1_alu_result));
  Register #(.width(32)) register_56 (.D(mem_stage_1_current_pc), .clk(clk), .Q(register_56_q), .clr(rst));  // open: en
  Register #(.width(32)) register_57 (
    .D(mem_stage_1_mem_sign_dout), .clk(clk), .Q(register_57_q), .clr(rst));  // open: en
  Register #(.width(1)) register_58 (.D(mem_stage_1_wb_en_wb), .clk(clk), .Q(ifwrite_pre_2), .clr(rst));  // open: en
  Register #(.width(5)) register_59 (.D(mem_stage_1_wb_addr_wb), .clk(clk), .Q(rd_pre_2), .clr(rst));  // open: en
  Register #(.width(2)) register_60 (.D(mem_stage_1_wbsel_wb), .clk(clk), .Q(register_60_q), .clr(rst));  // open: en
  Register #(.width(32)) register_61 (.D(mem_stage_1_alu_result), .clk(clk), .Q(register_61_q), .clr(rst));  // open: en
  WB_stage wb_stage_1 (
    .current_pc(register_56_q), .mem_sign_dout(register_57_q), .wb_en_wb(ifwrite_pre_2),
    .wb_addr_wb(rd_pre_2), .RST(rst), .WBSel_wb(register_60_q), .alu_result(register_61_q),
    .wb_data(wb_data_wb), .wb_addr(wb_addr_wb), .wb_en(wb_en_wb));

  // Notes on the sheet:
  //   DON'T TOUCH!
  //   IF stage output
  //   MEM stage output
  //   WB stage output
endmodule

module testbench (
  input  rst,
  output [7:0] out_2,
  output [31:0] current_pc_if,
  output mem_wen_mem,
  output halt,
  output [31:0] mem_din_mem,
  output [31:0] mem_dout_mem,
  output [31:0] mem_addr_mem,
  output control_en_mem,
  output [31:0] control_pc_mem,
  output wb_en_wb,
  output [4:0] wb_addr_wb,
  output [31:0] wb_data_wb
);

  wire and_1_out, carry, clk, not_1_out, not_2_out, por_1_out, rst_t;
  wire [31:0] inst;

  not not_1 (not_1_out, inst[2]);
  not not_2 (not_2_out, inst[3]);
  POR por_1 (.out(por_1_out));
  TOP top_1 (
    .clk(clk), .rst(rst_t), .inst(inst), .current_pc_if(current_pc_if), .mem_wen_mem(mem_wen_mem),
    .mem_din_mem(mem_din_mem), .mem_dout_mem(mem_dout_mem), .mem_addr_mem(mem_addr_mem),
    .control_en_mem(control_en_mem), .control_pc_mem(control_pc_mem), .wb_en_wb(wb_en_wb),
    .wb_addr_wb(wb_addr_wb), .wb_data_wb(wb_data_wb));
  Clock clock_1 (.out(clk));
  or or_1 (rst_t, rst, por_1_out);
  and and_1 (and_1_out, inst[0], inst[1], not_1_out, not_2_out, inst[4], inst[5], inst[6]);
  or or_2 (halt, and_1_out, carry);
  Counter counter_1 (.clr(rst_t), .up(1'b1), .count(1'b1), .clk(clk), .carry(carry), .Q(out_2));  // open: load, D
  // ROM #(.line("quad"), .misaligned("true")) rom_1: pin names not known; wires that end beside it: current_pc_if[7:0], inst[7:0], inst[15:8], inst[23:16], inst[31:24]
  // Probe on inst

  // Notes on the sheet:
  //   DON'T TOUCH!
  //   contents of rom_1 (hex, n*v repeats v):
  //   93 0 f0 ff 23 11 10 0 3 11 20 0 33 0 0 0 93 1 41
  //   IF stage output
  //   MEM stage output
  //   WB stage output
  //   test
endmodule

module regfile (
  input  [4:0] Read_Register_1_rs1,
  input  [4:0] Read_Register_2_rs2,
  input  [4:0] Write_Register_rd,
  input  [31:0] Write_Data,
  input  Write_Enable,
  input  Clock,
  input  RST,
  output [31:0] ra,
  output [31:0] sp,
  output [31:0] t0,
  output [31:0] t1,
  output [31:0] t2,
  output [31:0] s0,
  output [31:0] s1,
  output [31:0] a0,
  output [31:0] Read_Data_1,
  output [31:0] Read_Data_2
);

  wire comparator_1_eq, comparator_2_eq, demultiplexer_1_out1, demultiplexer_1_out2, demultiplexer_1_out3,
       demultiplexer_1_out4, demultiplexer_1_out5, demultiplexer_1_out6, demultiplexer_1_out7,
       demultiplexer_1_out8, demultiplexer_1_out9, demultiplexer_1_out10, demultiplexer_1_out11,
       demultiplexer_1_out12, demultiplexer_1_out13, demultiplexer_1_out14, demultiplexer_1_out15,
       demultiplexer_1_out16, demultiplexer_1_out17, demultiplexer_1_out18, demultiplexer_1_out19,
       demultiplexer_1_out20, demultiplexer_1_out21, demultiplexer_1_out22, demultiplexer_1_out23,
       demultiplexer_1_out24, demultiplexer_1_out25, demultiplexer_1_out26, demultiplexer_1_out27,
       demultiplexer_1_out28, demultiplexer_1_out29, demultiplexer_1_out30, demultiplexer_1_out31;
  wire [31:0] a1, a2, a3, a4, a5, a6, a7, gp, read_data1_1, read_data2_1, s2, s3, s4, s5, s6, s7, s8, s9,
       s10, s11, t3, t4, t5, t6, tp;

  Demultiplexer #(.select(5)) demultiplexer_1 (
    .out1(demultiplexer_1_out1), .out2(demultiplexer_1_out2), .out3(demultiplexer_1_out3),
    .out4(demultiplexer_1_out4), .out5(demultiplexer_1_out5), .out6(demultiplexer_1_out6),
    .out7(demultiplexer_1_out7), .out8(demultiplexer_1_out8), .out9(demultiplexer_1_out9),
    .out10(demultiplexer_1_out10), .out11(demultiplexer_1_out11), .out12(demultiplexer_1_out12),
    .out13(demultiplexer_1_out13), .out14(demultiplexer_1_out14), .out15(demultiplexer_1_out15),
    .out16(demultiplexer_1_out16), .out17(demultiplexer_1_out17), .out18(demultiplexer_1_out18),
    .out19(demultiplexer_1_out19), .out20(demultiplexer_1_out20), .out21(demultiplexer_1_out21),
    .out22(demultiplexer_1_out22), .out23(demultiplexer_1_out23), .out24(demultiplexer_1_out24),
    .out25(demultiplexer_1_out25), .out26(demultiplexer_1_out26), .out27(demultiplexer_1_out27),
    .out28(demultiplexer_1_out28), .out29(demultiplexer_1_out29), .out30(demultiplexer_1_out30),
    .out31(demultiplexer_1_out31), .in(Write_Enable), .sel(Write_Register_rd));  // open: out0
  Register #(.trigger("falling"), .width(32)) register_1 (
    .D(Write_Data), .en(demultiplexer_1_out1), .clk(Clock), .Q(ra), .clr(RST));
  Register #(.trigger("falling"), .width(32)) register_2 (
    .D(Write_Data), .en(demultiplexer_1_out2), .clk(Clock), .Q(sp), .clr(RST));
  Register #(.trigger("falling"), .width(32)) register_3 (
    .D(Write_Data), .en(demultiplexer_1_out3), .clk(Clock), .Q(gp), .clr(RST));
  Register #(.trigger("falling"), .width(32)) register_4 (
    .D(Write_Data), .en(demultiplexer_1_out4), .clk(Clock), .Q(tp), .clr(RST));
  Register #(.trigger("falling"), .width(32)) register_5 (
    .D(Write_Data), .en(demultiplexer_1_out5), .clk(Clock), .Q(t0), .clr(RST));
  Register #(.trigger("falling"), .width(32)) register_6 (
    .D(Write_Data), .en(demultiplexer_1_out6), .clk(Clock), .Q(t1), .clr(RST));
  Register #(.trigger("falling"), .width(32)) register_7 (
    .D(Write_Data), .en(demultiplexer_1_out7), .clk(Clock), .Q(t2), .clr(RST));
  Register #(.trigger("falling"), .width(32)) register_8 (
    .D(Write_Data), .en(demultiplexer_1_out8), .clk(Clock), .Q(s0), .clr(RST));
  Register #(.trigger("falling"), .width(32)) register_9 (
    .D(Write_Data), .en(demultiplexer_1_out9), .clk(Clock), .Q(s1), .clr(RST));
  Register #(.trigger("falling"), .width(32)) register_10 (
    .D(Write_Data), .en(demultiplexer_1_out10), .clk(Clock), .Q(a0), .clr(RST));
  Register #(.trigger("falling"), .width(32)) register_11 (
    .D(Write_Data), .en(demultiplexer_1_out11), .clk(Clock), .Q(a1), .clr(RST));
  Register #(.trigger("falling"), .width(32)) register_12 (
    .D(Write_Data), .en(demultiplexer_1_out12), .clk(Clock), .Q(a2), .clr(RST));
  Register #(.trigger("falling"), .width(32)) register_13 (
    .D(Write_Data), .en(demultiplexer_1_out13), .clk(Clock), .Q(a3), .clr(RST));
  Register #(.trigger("falling"), .width(32)) register_14 (
    .D(Write_Data), .en(demultiplexer_1_out14), .clk(Clock), .Q(a4), .clr(RST));
  Register #(.trigger("falling"), .width(32)) register_15 (
    .D(Write_Data), .en(demultiplexer_1_out15), .clk(Clock), .Q(a5), .clr(RST));
  Register #(.trigger("falling"), .width(32)) register_16 (
    .D(Write_Data), .en(demultiplexer_1_out16), .clk(Clock), .Q(a6), .clr(RST));
  Register #(.trigger("falling"), .width(32)) register_17 (
    .D(Write_Data), .en(demultiplexer_1_out17), .clk(Clock), .Q(a7), .clr(RST));
  Register #(.trigger("falling"), .width(32)) register_18 (
    .D(Write_Data), .en(demultiplexer_1_out18), .clk(Clock), .Q(s2), .clr(RST));
  Register #(.trigger("falling"), .width(32)) register_19 (
    .D(Write_Data), .en(demultiplexer_1_out19), .clk(Clock), .Q(s3), .clr(RST));
  Register #(.trigger("falling"), .width(32)) register_20 (
    .D(Write_Data), .en(demultiplexer_1_out20), .clk(Clock), .Q(s4), .clr(RST));
  Register #(.trigger("falling"), .width(32)) register_21 (
    .D(Write_Data), .en(demultiplexer_1_out21), .clk(Clock), .Q(s5), .clr(RST));
  Register #(.trigger("falling"), .width(32)) register_22 (
    .D(Write_Data), .en(demultiplexer_1_out22), .clk(Clock), .Q(s6), .clr(RST));
  Register #(.trigger("falling"), .width(32)) register_23 (
    .D(Write_Data), .en(demultiplexer_1_out23), .clk(Clock), .Q(s7), .clr(RST));
  Register #(.trigger("falling"), .width(32)) register_24 (
    .D(Write_Data), .en(demultiplexer_1_out24), .clk(Clock), .Q(s8), .clr(RST));
  Register #(.trigger("falling"), .width(32)) register_25 (
    .D(Write_Data), .en(demultiplexer_1_out25), .clk(Clock), .Q(s9), .clr(RST));
  Register #(.trigger("falling"), .width(32)) register_26 (
    .D(Write_Data), .en(demultiplexer_1_out26), .clk(Clock), .Q(s10), .clr(RST));
  Register #(.trigger("falling"), .width(32)) register_27 (
    .D(Write_Data), .en(demultiplexer_1_out27), .clk(Clock), .Q(s11), .clr(RST));
  Register #(.trigger("falling"), .width(32)) register_28 (
    .D(Write_Data), .en(demultiplexer_1_out28), .clk(Clock), .Q(t3), .clr(RST));
  Register #(.trigger("falling"), .width(32)) register_29 (
    .D(Write_Data), .en(demultiplexer_1_out29), .clk(Clock), .Q(t4), .clr(RST));
  Register #(.trigger("falling"), .width(32)) register_30 (
    .D(Write_Data), .en(demultiplexer_1_out30), .clk(Clock), .Q(t5), .clr(RST));
  Register #(.trigger("falling"), .width(32)) register_31 (
    .D(Write_Data), .en(demultiplexer_1_out31), .clk(Clock), .Q(t6), .clr(RST));
  Comparator #(.width(5)) comparator_1 (
    .a(Write_Register_rd), .b(Read_Register_1_rs1), .eq(comparator_1_eq));  // open: gt, lt
  Comparator #(.width(5)) comparator_2 (
    .a(Write_Register_rd), .b(Read_Register_2_rs2), .eq(comparator_2_eq));  // open: gt, lt
  Multiplexer #(.width(32)) multiplexer_1 (
    .in0(Read_Data_1), .in1(Write_Data), .out(read_data1_1), .sel(comparator_1_eq));
  Multiplexer #(.width(32)) multiplexer_2 (
    .in0(Read_Data_1), .in1(Write_Data), .out(read_data2_1), .sel(comparator_2_eq));
  Multiplexer #(.select(5), .width(32)) multiplexer_3 (
    .in0({32{1'b0}}), .in1(ra), .in2(sp), .in3(gp), .in4(tp), .in5(t0), .in6(t1), .in7(t2), .in8(s0),
    .in9(s1), .in10(a0), .in11(a1), .in12(a2), .in13(a3), .in14(a4), .in15(a5), .in16(a6), .in17(a7),
    .in18(s2), .in19(s3), .in20(s4), .in21(s5), .in22(s6), .in23(s7), .in24(s8), .in25(s9), .in26(s10),
    .in27(s11), .in28(t3), .in29(t4), .in30(t5), .in31(t6), .out(Read_Data_1), .sel(Read_Register_1_rs1));
  Multiplexer #(.select(5), .width(32)) multiplexer_4 (
    .in0({32{1'b0}}), .in1(ra), .in2(sp), .in3(gp), .in4(tp), .in5(t0), .in6(t1), .in7(t2), .in8(s0),
    .in9(s1), .in10(a0), .in11(a1), .in12(a2), .in13(a3), .in14(a4), .in15(a5), .in16(a6), .in17(a7),
    .in18(s2), .in19(s3), .in20(s4), .in21(s5), .in22(s6), .in23(s7), .in24(s8), .in25(s9), .in26(s10),
    .in27(s11), .in28(t3), .in29(t4), .in30(t5), .in31(t6), .out(Read_Data_2), .sel(Read_Register_2_rs2));

  // Other names for the same wires on the sheet: clk = Clock; read_data1[31:0] = Read_Data_1;
  //   read_data2[31:0] = Read_Data_2; read_reg1[4:0] = Read_Register_1_rs1; read_reg2[4:0] = Read_Register_2_rs2;
  //   write_en = Write_Enable; write_reg[4:0] = Write_Register_rd
endmodule

module DMEM (
  input  mem_ren,
  input  [31:0] WriteAddr,
  input  [31:0] WriteData,
  input  MemRW,
  input  clk,
  input  rst,
  input  is_sh,
  output [31:0] ReadData
);

  wire MemRW00, MemRW01, MemRW10, MemRW11, multiplexer_1_out, multiplexer_2_out, multiplexer_3_out,
       multiplexer_4_out, not_1_out;
  wire [7:0] multiplexer_9_out, multiplexer_10_out, multiplexer_11_out, multiplexer_12_out, out_1, out_2,
       out_3, out_4, WriteData00, WriteData01, WriteData10, WriteData11;
  wire [31:0] WriteAddr00, WriteAddr01, WriteAddr1, WriteAddr2, WriteAddr3, WriteAddr10, WriteAddr11;

  Multiplexer #(.select(2)) multiplexer_1 (
    .in0(1'b1), .in1(1'b0), .in2(1'b0), .in3(1'b1), .out(multiplexer_1_out), .sel(WriteAddr[1:0]));
  Multiplexer #(.select(2)) multiplexer_2 (
    .in0(1'b1), .in1(1'b1), .in2(1'b0), .in3(1'b0), .out(multiplexer_2_out), .sel(WriteAddr[1:0]));
  Multiplexer #(.select(2)) multiplexer_3 (
    .in0(1'b0), .in1(1'b1), .in2(1'b1), .in3(1'b0), .out(multiplexer_3_out), .sel(WriteAddr[1:0]));
  Multiplexer #(.select(2)) multiplexer_4 (
    .in0(1'b0), .in1(1'b0), .in2(1'b1), .in3(1'b1), .out(multiplexer_4_out), .sel(WriteAddr[1:0]));
  RAM #(.addrWidth(16), .asyncread("true"), .clearpin("true")) ram_1 (
    .addr(WriteAddr00[15:0]), .we(MemRW00), .oe(mem_ren), .clk(clk), .din(WriteData00), .dout(out_1),
    .clr(rst));
  Multiplexer multiplexer_5 (.in0(multiplexer_1_out), .in1(MemRW), .out(MemRW00), .sel(not_1_out));
  Multiplexer multiplexer_6 (.in0(multiplexer_2_out), .in1(MemRW), .out(MemRW01), .sel(not_1_out));
  Multiplexer multiplexer_7 (.in0(multiplexer_4_out), .in1(MemRW), .out(MemRW11), .sel(not_1_out));
  not not_1 (not_1_out, is_sh);
  Multiplexer multiplexer_8 (.in0(multiplexer_3_out), .in1(MemRW), .out(MemRW10), .sel(not_1_out));
  Adder #(.width(32)) adder_1 (.a(WriteAddr), .b(32'h1), .out(WriteAddr1));  // open: cin, cout
  Multiplexer #(.select(2), .width(8)) multiplexer_9 (
    .in0(out_1), .in1(out_2), .in2(out_3), .in3(out_4), .out(multiplexer_9_out), .sel(WriteAddr[1:0]));
  Multiplexer #(.select(2), .width(8)) multiplexer_10 (
    .in0(out_2), .in1(out_3), .in2(out_4), .in3(out_1), .out(multiplexer_10_out), .sel(WriteAddr[1:0]));
  Multiplexer #(.select(2), .width(8)) multiplexer_11 (
    .in0(out_3), .in1(out_4), .in2(out_1), .in3(out_2), .out(multiplexer_11_out), .sel(WriteAddr[1:0]));
  Multiplexer #(.select(2), .width(8)) multiplexer_12 (
    .in0(out_4), .in1(out_1), .in2(out_2), .in3(out_3), .out(multiplexer_12_out), .sel(WriteAddr[1:0]));
  Multiplexer #(.select(2), .width(32)) multiplexer_13 (
    .in0(WriteAddr), .in1(WriteAddr3), .in2(WriteAddr2), .in3(WriteAddr1), .out(WriteAddr00),
    .sel(WriteAddr[1:0]));
  Multiplexer #(.select(2), .width(32)) multiplexer_14 (
    .in0(WriteAddr1), .in1(WriteAddr), .in2(WriteAddr3), .in3(WriteAddr2), .out(WriteAddr01),
    .sel(WriteAddr[1:0]));
  Multiplexer #(.select(2), .width(32)) multiplexer_15 (
    .in0(WriteAddr2), .in1(WriteAddr1), .in2(WriteAddr), .in3(WriteAddr3), .out(WriteAddr10),
    .sel(WriteAddr[1:0]));
  Multiplexer #(.select(2), .width(32)) multiplexer_16 (
    .in0(WriteAddr3), .in1(WriteAddr2), .in2(WriteAddr1), .in3(WriteAddr), .out(WriteAddr11),
    .sel(WriteAddr[1:0]));
  RAM #(.addrWidth(16), .asyncread("true"), .clearpin("true")) meme (
    .addr(WriteAddr01[15:0]), .we(MemRW01), .oe(mem_ren), .clk(clk), .din(WriteData01), .dout(out_2),
    .clr(rst));
  Adder #(.width(32)) adder_2 (.a(WriteAddr1), .b(32'h1), .out(WriteAddr2));  // open: cin, cout
  Adder #(.width(32)) adder_3 (.a(WriteAddr2), .b(32'h1), .out(WriteAddr3));  // open: cin, cout
  Multiplexer #(.width(32)) multiplexer_17 (
    .in0({32{1'b0}}), .in1({multiplexer_12_out, multiplexer_11_out, multiplexer_10_out, multiplexer_9_out}),
    .out(ReadData), .sel(mem_ren));
  Multiplexer #(.select(2), .width(8)) multiplexer_18 (
    .in0(WriteData[7:0]), .in1(WriteData[31:24]), .in2(WriteData[23:16]), .in3(WriteData[15:8]),
    .out(WriteData00), .sel(WriteAddr[1:0]));
  Multiplexer #(.select(2), .width(8)) multiplexer_19 (
    .in0(WriteData[15:8]), .in1(WriteData[7:0]), .in2(WriteData[31:24]), .in3(WriteData[23:16]),
    .out(WriteData01), .sel(WriteAddr[1:0]));
  Multiplexer #(.select(2), .width(8)) multiplexer_20 (
    .in0(WriteData[23:16]), .in1(WriteData[15:8]), .in2(WriteData[7:0]), .in3(WriteData[31:24]),
    .out(WriteData10), .sel(WriteAddr[1:0]));
  Multiplexer #(.select(2), .width(8)) multiplexer_21 (
    .in0(WriteData[31:24]), .in1(WriteData[23:16]), .in2(WriteData[15:8]), .in3(WriteData[7:0]),
    .out(WriteData11), .sel(WriteAddr[1:0]));
  RAM #(.addrWidth(16), .asyncread("true"), .clearpin("true")) ram_2 (
    .addr(WriteAddr10[15:0]), .we(MemRW10), .oe(mem_ren), .clk(clk), .din(WriteData10), .dout(out_3),
    .clr(rst));
  RAM #(.addrWidth(16), .asyncread("true"), .clearpin("true")) ram_3 (
    .addr(WriteAddr11[15:0]), .we(MemRW11), .oe(mem_ren), .clk(clk), .din(WriteData11), .dout(out_4),
    .clr(rst));

  // Other names for the same wires on the sheet: SH = is_sh; SelOut0[1:0] = WriteAddr[1:0];
  //   WriteData1[7:0] = WriteData[7:0]; WriteData2[7:0] = WriteData[15:8]; WriteData3[7:0] = WriteData[23:16];
  //   WriteData4[7:0] = WriteData[31:24]

  // Notes on the sheet:
  //   lowest 8 bytes
  //   second lowest
  //   OUTPUT
endmodule

module ALU (
  input  [31:0] A,
  input  [31:0] B,
  input  [3:0] ALUSel,
  output [31:0] Result
);

  wire [0:0] slt13, sltiu15;
  wire [31:0] add3, and0, or1, sll14, sra12, srl11, sub4, xor2;

  assign and0 = A & B;  // AND_Gate and_1, 32 bits wide
  Adder #(.width(32)) adder_1 (.a(A), .b(B), .out(add3));  // open: cin, cout
  Shifter #(.shift("lr"), .width(32)) shifter_1 (.in(A), .\dist (B[4:0]), .out(srl11));
  Shifter #(.shift("ar"), .width(32)) shifter_2 (.in(A), .\dist (B[4:0]), .out(sra12));
  Shifter #(.width(32)) shifter_3 (.in(A), .\dist (B[4:0]), .out(sll14));
  assign or1 = A | B;  // OR_Gate or_1, 32 bits wide
  Subtractor #(.width(32)) subtractor_1 (.a(A), .b(B), .out(sub4));  // open: bin, bout
  Comparator #(.width(32)) comparator_1 (.a(A), .b(B), .lt(slt13[0]));  // open: gt, eq
  Comparator #(.mode("unsigned"), .width(32)) comparator_2 (.a(A), .b(B), .lt(sltiu15[0]));  // open: gt, eq
  assign xor2 = A ^ B;  // XOR_Gate xor_1, 32 bits wide
  Multiplexer #(.select(4), .width(32)) multiplexer_1 (
    .in0(and0), .in1(or1), .in2(xor2), .in3(add3), .in4(sub4), .in11(srl11), .in12(sra12),
    .in13({{31{1'b0}}, slt13[0]}), .in14(sll14), .in15({{31{1'b0}}, sltiu15[0]}), .out(Result), .sel(ALUSel));  // open: in5, in6, in7, in8, in9, in10

  // Notes on the sheet:
  //   INPUTS
  //   OUTPUT 
endmodule

module control (
  input  [31:0] Instruction,
  output [2:0] ImmSel,
  output control_en,
  output [1:0] ASel,
  output BSel,
  output [3:0] ALUSel,
  output MemRW,
  output reg_en,
  output [1:0] WBSel,
  output mem_ren,
  output if_sh,
  output read1,
  output read2,
  output is_SB,
  output islw
);

  wire and_7_out, and_8_out, and_9_out, and_10_out, and_11_out, and_12_out, and_13_out, and_14_out,
       and_15_out, and_16_out, and_17_out, and_18_out, and_19_out, and_20_out, comparator_1_eq,
       comparator_2_eq, comparator_3_eq, comparator_4_eq, comparator_5_eq, comparator_6_eq, comparator_7_eq,
       comparator_8_eq, comparator_9_eq, comparator_10_eq, comparator_11_eq, comparator_12_eq,
       comparator_13_eq, comparator_14_eq, comparator_15_eq, comparator_16_eq, comparator_17_eq,
       comparator_18_eq, comparator_19_eq, comparator_20_eq, comparator_21_eq, comparator_31_eq,
       comparator_32_eq, comparator_33_eq, comparator_34_eq, comparator_35_eq, comparator_36_eq,
       comparator_37_eq, comparator_38_eq, comparator_39_eq, comparator_40_eq, comparator_41_eq,
       comparator_42_eq, comparator_43_eq, comparator_44_eq, I_type_13, I_type_67, not_1_out, not_2_out,
       or_1_out, or_2_out, or_5_out, or_6_out, or_7_out, or_8_out, or_9_out, or_18_out, R_type, U_type_17,
       U_type_37, UJ_type;
  wire [1:0] and_24_out, and_25_out, bit_extender_6_out, bit_extender_10_out, multiplexer_23_out,
       multiplexer_24_out;
  wire [2:0] and_2_out, and_3_out, and_4_out, and_5_out, and_6_out, and_26_out, and_27_out, and_28_out,
       and_29_out, and_30_out, bit_extender_1_out, bit_extender_2_out, bit_extender_3_out,
       bit_extender_4_out, bit_extender_5_out, bit_extender_11_out, bit_extender_12_out, bit_extender_13_out,
       bit_extender_14_out, bit_extender_15_out;
  wire [3:0] and_21_out, and_22_out, and_23_out, bit_extender_7_out, bit_extender_8_out, bit_extender_9_out,
       I_ALUSel, multiplexer_1_out, multiplexer_2_out, multiplexer_3_out, multiplexer_4_out,
       multiplexer_5_out, multiplexer_6_out, multiplexer_7_out, multiplexer_8_out, multiplexer_9_out,
       multiplexer_10_out, multiplexer_11_out, multiplexer_12_out, multiplexer_13_out, multiplexer_14_out,
       multiplexer_15_out, multiplexer_16_out, multiplexer_17_out, multiplexer_18_out, multiplexer_19_out,
       multiplexer_20_out, multiplexer_21_out, multiplexer_22_out, R_ALUSel;

  Comparator #(.width(3)) comparator_1 (.a(Instruction[14:12]), .b(3'b000), .eq(comparator_1_eq));  // open: gt, lt
  Comparator #(.width(3)) comparator_2 (.a(Instruction[14:12]), .b(3'b100), .eq(comparator_2_eq));  // open: gt, lt
  Comparator #(.width(3)) comparator_3 (.a(Instruction[14:12]), .b(3'b110), .eq(comparator_3_eq));  // open: gt, lt
  Comparator #(.width(3)) comparator_4 (.a(Instruction[14:12]), .b(3'b001), .eq(comparator_4_eq));  // open: gt, lt
  Comparator #(.width(3)) comparator_5 (.a(Instruction[14:12]), .b(3'b111), .eq(comparator_5_eq));  // open: gt, lt
  Comparator #(.width(3)) comparator_6 (.a(Instruction[14:12]), .b(3'b000), .eq(comparator_6_eq));  // open: gt, lt
  Comparator #(.width(3)) comparator_7 (.a(Instruction[14:12]), .b(3'b001), .eq(comparator_7_eq));  // open: gt, lt
  Comparator #(.width(3)) comparator_8 (.a(Instruction[14:12]), .b(3'b010), .eq(comparator_8_eq));  // open: gt, lt
  Comparator #(.width(3)) comparator_9 (.a(Instruction[14:12]), .b(3'b100), .eq(comparator_9_eq));  // open: gt, lt
  Comparator #(.width(3)) comparator_10 (.a(Instruction[14:12]), .b(3'b101), .eq(comparator_10_eq));  // open: gt, lt
  Comparator #(.width(3)) comparator_11 (.a(Instruction[14:12]), .b(3'b110), .eq(comparator_11_eq));  // open: gt, lt
  Comparator #(.width(3)) comparator_12 (.a(Instruction[14:12]), .b(3'b111), .eq(comparator_12_eq));  // open: gt, lt
  Comparator #(.width(3)) comparator_13 (.a(Instruction[14:12]), .b(3'b000), .eq(comparator_13_eq));  // open: gt, lt
  Comparator #(.width(3)) comparator_14 (.a(Instruction[14:12]), .b(3'b001), .eq(comparator_14_eq));  // open: gt, lt
  Comparator #(.width(3)) comparator_15 (.a(Instruction[14:12]), .b(3'b011), .eq(comparator_15_eq));  // open: gt, lt
  Comparator #(.width(3)) comparator_16 (.a(Instruction[14:12]), .b(3'b100), .eq(comparator_16_eq));  // open: gt, lt
  Comparator #(.width(3)) comparator_17 (.a(Instruction[14:12]), .b(3'b101), .eq(comparator_17_eq));  // open: gt, lt
  Comparator #(.width(3)) comparator_18 (.a(Instruction[14:12]), .b(3'b110), .eq(comparator_18_eq));  // open: gt, lt
  Comparator #(.width(3)) comparator_19 (.a(Instruction[14:12]), .b(3'b111), .eq(comparator_19_eq));  // open: gt, lt
  Comparator #(.width(3)) comparator_20 (.a(Instruction[14:12]), .b(3'b010), .eq(comparator_20_eq));  // open: gt, lt
  Comparator #(.width(3)) comparator_21 (.a(Instruction[14:12]), .b(3'b001), .eq(comparator_21_eq));  // open: gt, lt
  or or_1 (or_1_out, islw, I_type_13, I_type_67);
  or or_2 (or_2_out, U_type_17, U_type_37);
  Multiplexer #(.width(4)) multiplexer_1 (.in0(4'b0000), .in1(4'b0011), .out(multiplexer_1_out), .sel(comparator_6_eq));
  Multiplexer #(.width(4)) multiplexer_2 (.in0(4'b0000), .in1(4'b1110), .out(multiplexer_2_out), .sel(comparator_7_eq));
  Multiplexer #(.width(4)) multiplexer_3 (.in0(4'b0000), .in1(4'b1101), .out(multiplexer_3_out), .sel(comparator_8_eq));
  Multiplexer #(.width(4)) multiplexer_4 (.in0(4'b0000), .in1(4'b0010), .out(multiplexer_4_out), .sel(comparator_9_eq));
  Multiplexer #(.width(4)) multiplexer_5 (
    .in0(4'b0000), .in1(4'b1011), .out(multiplexer_5_out), .sel(comparator_10_eq));
  Multiplexer #(.width(4)) multiplexer_6 (
    .in0(4'b0000), .in1(4'b0001), .out(multiplexer_6_out), .sel(comparator_11_eq));
  Multiplexer #(.width(4)) multiplexer_7 (
    .in0(4'b0000), .in1(4'b0000), .out(multiplexer_7_out), .sel(comparator_12_eq));
  Multiplexer #(.width(4)) multiplexer_8 (
    .in0(4'b0000), .in1(4'b1111), .out(multiplexer_8_out), .sel(comparator_15_eq));
  and and_1 (if_sh, MemRW, comparator_21_eq);
  Comparator #(.width(7)) comparator_22 (.a(Instruction[6:0]), .b(7'b0110011), .eq(R_type));  // open: gt, lt
  Comparator #(.width(7)) comparator_23 (.a(Instruction[6:0]), .b(7'b0000011), .eq(islw));  // open: gt, lt
  Comparator #(.width(7)) comparator_24 (.a(Instruction[6:0]), .b(7'b0010011), .eq(I_type_13));  // open: gt, lt
  Comparator #(.width(7)) comparator_25 (.a(Instruction[6:0]), .b(7'b0100011), .eq(MemRW));  // open: gt, lt
  Comparator #(.width(7)) comparator_26 (.a(Instruction[6:0]), .b(7'b1100011), .eq(is_SB));  // open: gt, lt
  Comparator #(.width(7)) comparator_27 (.a(Instruction[6:0]), .b(7'b0010111), .eq(U_type_17));  // open: gt, lt
  Comparator #(.width(7)) comparator_28 (.a(Instruction[6:0]), .b(7'b0110111), .eq(U_type_37));  // open: gt, lt
  Comparator #(.width(7)) comparator_29 (.a(Instruction[6:0]), .b(7'b1101111), .eq(UJ_type));  // open: gt, lt
  Comparator #(.width(7)) comparator_30 (.a(Instruction[6:0]), .b(7'b1100111), .eq(I_type_67));  // open: gt, lt
  assign bit_extender_1_out = {{2{or_1_out}}, or_1_out};  // Bit_Extender bit_extender_1
  assign bit_extender_2_out = {{2{MemRW}}, MemRW};  // Bit_Extender bit_extender_2
  assign bit_extender_3_out = {{2{is_SB}}, is_SB};  // Bit_Extender bit_extender_3
  assign bit_extender_4_out = {{2{or_2_out}}, or_2_out};  // Bit_Extender bit_extender_4
  assign bit_extender_5_out = {{2{UJ_type}}, UJ_type};  // Bit_Extender bit_extender_5
  assign I_ALUSel = multiplexer_1_out | multiplexer_2_out | multiplexer_3_out | multiplexer_4_out | multiplexer_5_out | multiplexer_6_out | multiplexer_7_out | multiplexer_8_out;  // OR_Gate or_3, 4 bits wide
  assign and_2_out = bit_extender_1_out & 3'b000;  // AND_Gate and_2, 3 bits wide
  assign and_3_out = bit_extender_2_out & 3'b001;  // AND_Gate and_3, 3 bits wide
  assign and_4_out = bit_extender_3_out & 3'b010;  // AND_Gate and_4, 3 bits wide
  assign and_5_out = bit_extender_4_out & 3'b011;  // AND_Gate and_5, 3 bits wide
  assign and_6_out = bit_extender_5_out & 3'b100;  // AND_Gate and_6, 3 bits wide
  Comparator #(.width(7)) comparator_31 (.a(Instruction[31:25]), .b({7{1'b0}}), .eq(comparator_31_eq));  // open: gt, lt
  Comparator #(.width(7)) comparator_32 (
    .a(Instruction[31:25]), .b(7'b0000001), .eq(comparator_32_eq));  // open: gt, lt
  Comparator #(.width(7)) comparator_33 (
    .a(Instruction[31:25]), .b(7'b0100000), .eq(comparator_33_eq));  // open: gt, lt
  Comparator #(.width(7)) comparator_34 (.a(Instruction[31:25]), .b({7{1'b0}}), .eq(comparator_34_eq));  // open: gt, lt
  Comparator #(.width(7)) comparator_35 (
    .a(Instruction[31:25]), .b(7'b0000001), .eq(comparator_35_eq));  // open: gt, lt
  Comparator #(.width(7)) comparator_36 (
    .a(Instruction[31:25]), .b(7'b0000001), .eq(comparator_36_eq));  // open: gt, lt
  Comparator #(.width(7)) comparator_37 (.a(Instruction[31:25]), .b({7{1'b0}}), .eq(comparator_37_eq));  // open: gt, lt
  Comparator #(.width(7)) comparator_38 (
    .a(Instruction[31:25]), .b(7'b0000001), .eq(comparator_38_eq));  // open: gt, lt
  Comparator #(.width(7)) comparator_39 (
    .a(Instruction[31:25]), .b(7'b0100000), .eq(comparator_39_eq));  // open: gt, lt
  Comparator #(.width(7)) comparator_40 (.a(Instruction[31:25]), .b({7{1'b0}}), .eq(comparator_40_eq));  // open: gt, lt
  Comparator #(.width(7)) comparator_41 (.a(Instruction[31:25]), .b({7{1'b0}}), .eq(comparator_41_eq));  // open: gt, lt
  Comparator #(.width(7)) comparator_42 (
    .a(Instruction[31:25]), .b(7'b0000001), .eq(comparator_42_eq));  // open: gt, lt
  Comparator #(.width(7)) comparator_43 (.a(Instruction[31:25]), .b({7{1'b0}}), .eq(comparator_43_eq));  // open: gt, lt
  Comparator #(.width(7)) comparator_44 (.a(Instruction[31:25]), .b({7{1'b0}}), .eq(comparator_44_eq));  // open: gt, lt
  assign ImmSel = and_2_out | and_3_out | and_4_out | and_5_out | and_6_out;  // OR_Gate or_4, 3 bits wide
  and and_7 (and_7_out, comparator_13_eq, comparator_31_eq);
  and and_8 (and_8_out, comparator_13_eq, comparator_32_eq);
  and and_9 (and_9_out, comparator_13_eq, comparator_33_eq);
  and and_10 (and_10_out, comparator_14_eq, comparator_34_eq);
  and and_11 (and_11_out, comparator_14_eq, comparator_35_eq);
  and and_12 (and_12_out, comparator_15_eq, comparator_36_eq);
  and and_13 (and_13_out, comparator_16_eq, comparator_37_eq);
  and and_14 (and_14_out, comparator_16_eq, comparator_38_eq);
  and and_15 (and_15_out, comparator_17_eq, comparator_39_eq);
  and and_16 (and_16_out, comparator_17_eq, comparator_40_eq);
  and and_17 (and_17_out, comparator_18_eq, comparator_41_eq);
  and and_18 (and_18_out, comparator_19_eq, comparator_42_eq);
  and and_19 (and_19_out, comparator_19_eq, comparator_43_eq);
  and and_20 (and_20_out, comparator_20_eq, comparator_44_eq);
  Multiplexer #(.width(4)) multiplexer_9 (.in0(4'b0000), .in1(4'b0011), .out(multiplexer_9_out), .sel(and_7_out));
  Multiplexer #(.width(4)) multiplexer_10 (.in0(4'b0000), .in1(4'b0101), .out(multiplexer_10_out), .sel(and_8_out));
  Multiplexer #(.width(4)) multiplexer_11 (.in0(4'b0000), .in1(4'b0100), .out(multiplexer_11_out), .sel(and_9_out));
  Multiplexer #(.width(4)) multiplexer_12 (.in0(4'b0000), .in1(4'b1110), .out(multiplexer_12_out), .sel(and_10_out));
  Multiplexer #(.width(4)) multiplexer_13 (.in0(4'b0000), .in1(4'b0111), .out(multiplexer_13_out), .sel(and_11_out));
  Multiplexer #(.width(4)) multiplexer_14 (.in0(4'b0000), .in1(4'b0110), .out(multiplexer_14_out), .sel(and_12_out));
  Multiplexer #(.width(4)) multiplexer_15 (.in0(4'b0000), .in1(4'b0010), .out(multiplexer_15_out), .sel(and_13_out));
  Multiplexer #(.width(4)) multiplexer_16 (.in0(4'b0000), .in1(4'b1001), .out(multiplexer_16_out), .sel(and_14_out));
  Multiplexer #(.width(4)) multiplexer_17 (.in0(4'b0000), .in1(4'b1100), .out(multiplexer_17_out), .sel(and_15_out));
  Multiplexer #(.width(4)) multiplexer_18 (.in0(4'b0000), .in1(4'b1011), .out(multiplexer_18_out), .sel(and_16_out));
  Multiplexer #(.width(4)) multiplexer_19 (.in0(4'b0000), .in1(4'b0001), .out(multiplexer_19_out), .sel(and_17_out));
  Multiplexer #(.width(4)) multiplexer_20 (.in0(4'b0000), .in1(4'b1010), .out(multiplexer_20_out), .sel(and_18_out));
  Multiplexer #(.width(4)) multiplexer_21 (.in0(4'b0000), .in1(4'b0000), .out(multiplexer_21_out), .sel(and_19_out));
  Multiplexer #(.width(4)) multiplexer_22 (.in0(4'b0000), .in1(4'b1101), .out(multiplexer_22_out), .sel(and_20_out));
  or or_5 (or_5_out, R_type, U_type_17, U_type_37, I_type_13);
  or or_6 (or_6_out, I_type_13, R_type);
  assign bit_extender_6_out = {{1{or_7_out}}, or_7_out};  // Bit_Extender bit_extender_6
  or or_7 (or_7_out, is_SB, U_type_17, UJ_type);
  Multiplexer #(.width(2)) multiplexer_23 (.in0(2'b10), .in1(2'b01), .out(multiplexer_23_out), .sel(or_5_out));
  or or_8 (or_8_out, islw, I_type_13, I_type_67);
  or or_9 (or_9_out, U_type_17, U_type_37);
  assign bit_extender_7_out = {{3{not_1_out}}, not_1_out};  // Bit_Extender bit_extender_7
  not not_1 (not_1_out, or_6_out);
  assign bit_extender_8_out = {{3{R_type}}, R_type};  // Bit_Extender bit_extender_8
  assign bit_extender_9_out = {{3{I_type_13}}, I_type_13};  // Bit_Extender bit_extender_9
  assign R_ALUSel = multiplexer_9_out | multiplexer_10_out | multiplexer_11_out | multiplexer_12_out | multiplexer_13_out | multiplexer_14_out | multiplexer_16_out | multiplexer_17_out | multiplexer_18_out | multiplexer_19_out | multiplexer_20_out | multiplexer_21_out | multiplexer_22_out;  // OR_Gate or_10, 4 bits wide
  assign bit_extender_10_out = {{1{U_type_37}}, U_type_37};  // Bit_Extender bit_extender_10
  Multiplexer #(.width(2)) multiplexer_24 (.in0(multiplexer_23_out), .in1(2'b00), .out(multiplexer_24_out), .sel(islw));
  assign bit_extender_11_out = {{2{or_8_out}}, or_8_out};  // Bit_Extender bit_extender_11
  assign bit_extender_12_out = {{2{MemRW}}, MemRW};  // Bit_Extender bit_extender_12
  assign bit_extender_13_out = {{2{is_SB}}, is_SB};  // Bit_Extender bit_extender_13
  assign bit_extender_14_out = {{2{or_9_out}}, or_9_out};  // Bit_Extender bit_extender_14
  assign bit_extender_15_out = {{2{UJ_type}}, UJ_type};  // Bit_Extender bit_extender_15
  assign and_21_out = 4'b0011 & bit_extender_7_out;  // AND_Gate and_21, 4 bits wide
  assign and_22_out = R_ALUSel & bit_extender_8_out;  // AND_Gate and_22, 4 bits wide
  assign and_23_out = I_ALUSel & bit_extender_9_out;  // AND_Gate and_23, 4 bits wide
  assign and_24_out = bit_extender_6_out & 2'b01;  // AND_Gate and_24, 2 bits wide
  assign and_25_out = bit_extender_10_out & 2'b10;  // AND_Gate and_25, 2 bits wide
  or or_11 (mem_ren, islw, MemRW);
  or or_12 (read2, R_type, MemRW, is_SB);
  or or_13 (reg_en, I_type_67, R_type, islw, UJ_type, I_type_13, U_type_17, U_type_37);
  Multiplexer #(.width(2)) multiplexer_25 (.in0(multiplexer_24_out), .in1(2'b11), .out(WBSel), .sel(not_2_out));
  not not_2 (not_2_out, reg_en);
  assign and_26_out = bit_extender_11_out & 3'b000;  // AND_Gate and_26, 3 bits wide
  assign and_27_out = bit_extender_12_out & 3'b001;  // AND_Gate and_27, 3 bits wide
  assign and_28_out = bit_extender_13_out & 3'b010;  // AND_Gate and_28, 3 bits wide
  assign and_29_out = bit_extender_14_out & 3'b011;  // AND_Gate and_29, 3 bits wide
  assign and_30_out = bit_extender_15_out & 3'b100;  // AND_Gate and_30, 3 bits wide
  assign ALUSel = and_21_out | and_22_out | and_23_out;  // OR_Gate or_14, 4 bits wide
  not not_3 (BSel, R_type);
  assign ASel = and_24_out | and_25_out;  // OR_Gate or_15, 2 bits wide
  or or_16 (control_en, UJ_type, I_type_67);
  assign ImmSel = and_26_out | and_27_out | and_28_out | and_29_out | and_30_out;  // OR_Gate or_17, 3 bits wide
  or or_18 (or_18_out, islw, I_type_67, I_type_13);
  or or_19 (read1, R_type, MemRW, or_18_out, is_SB);

  // Other names for the same wires on the sheet: I_type_03 = islw; ifread_1 = read1; ifread_2 = read2;
  //   inst[31:0] = Instruction; Opcode[6:0] = Instruction[6:0]; funct3[2:0] = Instruction[14:12];
  //   funct7[6:0] = Instruction[31:25]; mem_wen = MemRW; S_type = MemRW; SB_type = is_SB; SH = if_sh; wb_en = reg_en

  // Notes on the sheet:
  //   ADD
endmodule

module imm_gen (
  input  [31:0] Inst,
  input  [2:0] Imm_sel,
  output [31:0] Imm
);

  wire [31:0] bit_extender_1_out, bit_extender_2_out, bit_extender_3_out, bit_extender_4_out,
       bit_extender_5_out;

  assign bit_extender_1_out = {{20{Inst[31]}}, Inst[31:20]};  // Bit_Extender bit_extender_1
  assign bit_extender_2_out = {{20{Inst[31]}}, {Inst[31:25], Inst[11:7]}};  // Bit_Extender bit_extender_2
  assign bit_extender_3_out = {{19{Inst[31]}}, {Inst[31], Inst[7], Inst[30:25], Inst[11:8], 1'b0}};  // Bit_Extender bit_extender_3
  Bit_Extender #(.in_width(32), .out_width(32)) bit_extender_4 (
    .in({Inst[31:12], {12{1'b0}}}), .out(bit_extender_4_out));
  assign bit_extender_5_out = {{11{Inst[31]}}, {Inst[31], Inst[19:12], Inst[20], Inst[30:21], 1'b0}};  // Bit_Extender bit_extender_5
  Multiplexer #(.select(3), .width(32)) multiplexer_1 (
    .in0(bit_extender_1_out), .in1(bit_extender_2_out), .in2(bit_extender_3_out), .in3(bit_extender_4_out),
    .in4(bit_extender_5_out), .out(Imm), .sel(Imm_sel));  // open: in5, in6, in7

  // Notes on the sheet:
  //   Take away opcode 0-6
  //   I-type
  //   S-type
  //   B-type
  //   U-type
  //   J-type
  //   Imm [11:0]
  //   Imm [4:0] Imm[11:5]
  //   Imm[31:12]
  //   Imm [4:1] Imm [11] Imm[10:5] Imm[12]
  //   Imm[19:12] Imm[11] Imm[10:1] Imm[20]
endmodule

module IF_stage (
  input  [31:0] current_pc,
  input  [31:0] control_pc_mem,
  input  [31:0] Instruction,
  input  RST,
  input  clk,
  input  control_en,
  output [31:0] current_pc_id,
  output control_en_mem,
  output [1:0] ASel,
  output BSel,
  output [3:0] ALUSel,
  output MemRW,
  output wb_en_wb,
  output [1:0] WBSel,
  output mem_ren,
  output if_sh,
  output [4:0] rs2,
  output [4:0] rs1,
  output [31:0] imm,
  output [4:0] rd,
  output read_1,
  output read_2,
  output [31:0] inst_id,
  output is_Sb,
  output is_I03
);

  wire control_1_control_en, control_1_memrw, control_1_reg_en;
  wire [0:0] multiplexer_4_out;
  wire [2:0] Imm_sel;
  wire [31:0] adder_1_out;

  control control_1 (
    .Instruction(Instruction), .ImmSel(Imm_sel), .control_en(control_1_control_en), .ASel(ASel), .BSel(BSel),
    .ALUSel(ALUSel), .MemRW(control_1_memrw), .reg_en(control_1_reg_en), .WBSel(WBSel), .mem_ren(mem_ren),
    .if_sh(if_sh), .read1(read_1), .read2(read_2), .is_SB(is_Sb), .islw(is_I03));
  Multiplexer multiplexer_1 (.in0(control_1_control_en), .in1(1'b0), .out(control_en_mem), .sel(RST));
  Multiplexer multiplexer_2 (.in0(control_1_memrw), .in1(1'b0), .out(MemRW), .sel(RST));
  Multiplexer multiplexer_3 (.in0(control_1_reg_en), .in1(1'b0), .out(wb_en_wb), .sel(RST));
  Adder #(.width(32)) adder_1 (.a(32'h4), .b(current_pc), .out(adder_1_out));  // open: cin, cout
  Multiplexer #(.width(32)) multiplexer_4 (
    .in0(adder_1_out), .in1({control_pc_mem[31:1], 1'b0}), .out({current_pc_id[31:1], multiplexer_4_out[0]}),
    .sel(control_en));
  imm_gen imm_gen_1 (.Inst(Instruction), .Imm_sel(Imm_sel), .Imm(imm));
  Multiplexer #(.width(5)) multiplexer_5 (.in0({5{1'b0}}), .in1(Instruction[11:7]), .out(rd), .sel(wb_en_wb));

  assign current_pc_id[0] = 1'b0;
  assign inst_id = Instruction;
  assign rs1 = Instruction[19:15];
  assign rs2 = Instruction[24:20];

  // Other names for the same wires on the sheet: current_pc_if[31:0] = current_pc; Gen_Imm[31:0] = imm;
  //   inst[31:0] = Instruction; write_rs1_addr[4:0] = Instruction[19:15]; write_rs2_addr[4:0] = Instruction[24:20];
  //   mem_wen_mem = MemRW; SH = if_sh; wb_addr_wb[4:0] = rd

  // Notes on the sheet:
  //   INPUTS
  //   OUTPUT 
endmodule

module ID_stage (
  input  [31:0] current_pc_id,
  input  control_en_id,
  input  [1:0] ASel,
  input  BSel,
  input  [3:0] ALUSel,
  input  MemRW,
  input  wb_en_id,
  input  [1:0] WBSel,
  input  mem_ren,
  input  if_sh,
  input  [4:0] rs2,
  input  [4:0] rs1,
  input  [31:0] imm,
  input  [4:0] rd_ex,
  input  [31:0] wb_data_wb,
  input  RST,
  input  clk,
  input  [4:0] rd_wb,
  input  wb_en_wb,
  input  re1,
  input  re2,
  input  [31:0] Instruction,
  input  issb,
  input  lw,
  output [31:0] control_pc_ex,
  output [31:0] r1,
  output [31:0] r2,
  output control_en_ex,
  output [1:0] ASel_ex,
  output BSel_ex,
  output [3:0] ALUSel_ex,
  output mem_wen_ex,
  output [1:0] wb_sel_ex,
  output is_sh_ex,
  output [31:0] imm_ex,
  output wb_en_ex,
  output mem_ren_ex,
  output [4:0] rd,
  output rea1,
  output rea2,
  output [31:0] inst,
  output is_sb,
  output is_i03
);

  regfile regfile_1 (
    .Read_Register_1_rs1(rs1), .Read_Register_2_rs2(rs2), .Write_Register_rd(rd_wb), .Write_Data(wb_data_wb),
    .Write_Enable(wb_en_wb), .Clock(clk), .RST(RST), .Read_Data_1(r1), .Read_Data_2(r2));  // open: ra, sp, t0, t1, t2, s0, s1, a0

  assign ALUSel_ex = ALUSel;
  assign ASel_ex = ASel;
  assign BSel_ex = BSel;
  assign control_en_ex = control_en_id;
  assign control_pc_ex = current_pc_id;
  assign imm_ex = imm;
  assign inst = Instruction;
  assign is_i03 = lw;
  assign is_sb = issb;
  assign is_sh_ex = if_sh;
  assign mem_ren_ex = mem_ren;
  assign mem_wen_ex = MemRW;
  assign rd = rd_ex;
  assign rea1 = re1;
  assign rea2 = re2;
  assign wb_en_ex = wb_en_id;
  assign wb_sel_ex = WBSel;

  // Other names for the same wires on the sheet: control_en_mem = control_en_id; current_pc_if[31:0] = current_pc_id;
  //   Gen_Imm[31:0] = imm; mem_wen_mem = MemRW; read_1 = re1; read_2 = re2; SH = if_sh; wb_addr_id[4:0] = rd_ex;
  //   wb_addr_wb[4:0] = rd_wb; write_rs1_addr[4:0] = rs1; write_rs2_addr[4:0] = rs2
endmodule

module EX_stage (
  input  [31:0] current_pc_ex,
  input  [31:0] r1,
  input  [31:0] r2,
  input  control_en_ex,
  input  [1:0] ASel_ex,
  input  BSel_ex,
  input  [3:0] ALUSel_ex,
  input  mem_wen_ex,
  input  [1:0] wb_sel_ex,
  input  is_sh_ex,
  input  [31:0] imm_ex,
  input  wb_en_ex,
  input  mem_ren_ex,
  input  [4:0] rd_ex,
  input  [31:0] Instruction,
  input  is_sb,
  input  is_lw,
  output [31:0] current_pc_mem,
  output [31:0] alu_result_mem,
  output control_en_mem,
  output mem_wen_mem,
  output [1:0] WBSel_mem,
  output is_sh_mem,
  output wb_en_mem,
  output mem_ren_mem,
  output [4:0] wb_addr_mem,
  output [31:0] mem_din_mem,
  output [31:0] control_pc_mem,
  output [31:0] mem_addr_mem,
  output [31:0] inst,
  output islw
);

  wire BrEq, comparator_1_eq, comparator_1_lt, comparator_2_lt;
  wire [0:0] multiplexer_1_out;
  wire [31:0] bit_extender_1_out, multiplexer_3_out, multiplexer_4_out, subtractor_1_out;

  Subtractor #(.width(32)) subtractor_1 (.a(current_pc_ex), .b(32'h4), .out(subtractor_1_out));  // open: bin, bout
  Multiplexer #(.width(32)) multiplexer_1 (
    .in0({32{1'b0}}), .in1(alu_result_mem), .out({control_pc_mem[31:1], multiplexer_1_out[0]}),
    .sel(control_en_mem));
  assign bit_extender_1_out = {{31{mem_wen_ex}}, mem_wen_ex};  // Bit_Extender bit_extender_1
  Multiplexer #(.width(32)) multiplexer_2 (
    .in0({32{1'b0}}), .in1(alu_result_mem), .out(mem_addr_mem), .sel(mem_ren_ex));
  assign mem_din_mem = bit_extender_1_out & r2;  // AND_Gate and_1, 32 bits wide
  Comparator #(.width(32)) comparator_1 (.a(r1), .b(r2), .eq(comparator_1_eq), .lt(comparator_1_lt));  // open: gt
  Comparator #(.mode("unsigned"), .width(32)) comparator_2 (.a(r1), .b(r2), .lt(comparator_2_lt));  // open: gt, eq
  Multiplexer #(.select(2), .width(32)) multiplexer_3 (
    .in0(r1), .in1(subtractor_1_out), .in2({32{1'b0}}), .out(multiplexer_3_out), .sel(ASel_ex));  // open: in3
  Multiplexer #(.width(32)) multiplexer_4 (.in0(r2), .in1(imm_ex), .out(multiplexer_4_out), .sel(BSel_ex));
  Multiplexer multiplexer_5 (.in0(comparator_1_lt), .in1(comparator_2_lt));  // open: out, sel
  Multiplexer multiplexer_6 (.in0(control_en_ex), .in1(1'b1), .out(control_en_mem), .sel(BrEq));
  and and_2 (BrEq, comparator_1_eq, is_sb);
  ALU alu_1 (.A(multiplexer_3_out), .B(multiplexer_4_out), .ALUSel(ALUSel_ex), .Result(alu_result_mem));

  assign control_pc_mem[0] = 1'b0;
  assign current_pc_mem = current_pc_ex;
  assign inst = Instruction;
  assign is_sh_mem = is_sh_ex;
  assign islw = is_lw;
  assign mem_ren_mem = mem_ren_ex;
  assign mem_wen_mem = mem_wen_ex;
  assign wb_addr_mem = rd_ex;
  assign wb_en_mem = wb_en_ex;
  assign WBSel_mem = wb_sel_ex;

  // Other names for the same wires on the sheet: alu_result[31:0] = alu_result_mem; ALUSel[3:0] = ALUSel_ex;
  //   ASel[1:0] = ASel_ex; BSel = BSel_ex; current_pc[31:0] = current_pc_ex; Gen_Imm[31:0] = imm_ex; is_I03 = is_lw;
  //   mem_ren = mem_ren_ex; SH = is_sh_ex; wb_addr_wb[4:0] = rd_ex; wb_en_wb = wb_en_ex; WBSel[1:0] = wb_sel_ex

  // Notes on the sheet:
  //   B type comparator
endmodule

module MEM_stage (
  input  [31:0] current_pc_mem,
  input  [31:0] alu_result_mem,
  input  control_en_mem,
  input  mem_wen_mem,
  input  [1:0] WBSel_mem,
  input  is_sh_mem,
  input  wb_en_mem,
  input  mem_ren_mem,
  input  [4:0] wb_addr_mem,
  input  [31:0] mem_din_mem,
  input  [31:0] control_pc_mem,
  input  [31:0] mem_addr_mem,
  input  RST,
  input  clk,
  input  [31:0] inst,
  output [31:0] current_pc,
  output [31:0] mem_dout,
  output [31:0] mem_sign_dout,
  output wb_en_wb,
  output [4:0] wb_addr_wb,
  output mem_wen,
  output [31:0] mem_din,
  output [31:0] control_pc,
  output control_en,
  output [31:0] mem_addr,
  output [1:0] WBSel_wb,
  output [31:0] alu_result
);

  wire [31:0] bit_extender_1_out, bit_extender_2_out;

  DMEM dmem_1 (
    .mem_ren(mem_ren_mem), .WriteAddr(mem_addr_mem), .WriteData(mem_din_mem), .MemRW(mem_wen_mem), .clk(clk),
    .rst(RST), .is_sh(is_sh_mem), .ReadData(mem_dout));
  assign bit_extender_1_out = {{16{mem_dout[15]}}, mem_dout[15:0]};  // Bit_Extender bit_extender_1
  Bit_Extender #(.in_width(32), .out_width(32)) bit_extender_2 (.in(mem_dout), .out(bit_extender_2_out));
  Multiplexer #(.select(3), .width(32)) multiplexer_1 (
    .in0({32{1'b0}}), .in1(bit_extender_1_out), .in2(bit_extender_2_out), .in3({32{1'b0}}), .in4({32{1'b0}}),
    .in7({32{1'b0}}), .out(mem_sign_dout), .sel(inst[14:12]));  // open: in5, in6

  assign alu_result = alu_result_mem;
  assign control_en = control_en_mem;
  assign control_pc = control_pc_mem;
  assign current_pc = current_pc_mem;
  assign mem_addr = mem_addr_mem;
  assign mem_din = mem_din_mem;
  assign mem_wen = mem_wen_mem;
  assign wb_addr_wb = wb_addr_mem;
  assign wb_en_wb = wb_en_mem;
  assign WBSel_wb = WBSel_mem;

  // Other names for the same wires on the sheet: current_pc_if[31:0] = current_pc_mem; Opcode[6:0] = inst[6:0];
  //   funct3[2:0] = inst[14:12]; funct7[6:0] = inst[31:25]; mem_dout_mem[31:0] = mem_dout; mem_ren = mem_ren_mem;
  //   SH = is_sh_mem; WBSel[1:0] = WBSel_mem

  // Notes on the sheet:
  //   MEM
endmodule

module WB_stage (
  input  [31:0] current_pc,
  input  [31:0] mem_sign_dout,
  input  wb_en_wb,
  input  [4:0] wb_addr_wb,
  input  RST,
  input  [1:0] WBSel_wb,
  input  [31:0] alu_result,
  output [31:0] wb_data,
  output [4:0] wb_addr,
  output wb_en
);

  wire [31:0] adder_1_out, multiplexer_1_out, subtractor_1_out;

  Subtractor #(.width(32)) subtractor_1 (.a(current_pc), .b(32'h4), .out(subtractor_1_out));  // open: bin, bout
  Adder #(.width(32)) adder_1 (.a(subtractor_1_out), .b(32'h4), .out(adder_1_out));  // open: cin, cout
  Multiplexer #(.select(2), .width(32)) multiplexer_1 (
    .in0(mem_sign_dout), .in1(alu_result), .in2(adder_1_out), .in3({32{1'b0}}), .out(multiplexer_1_out),
    .sel(WBSel_wb));
  Multiplexer #(.width(32)) multiplexer_2 (.in0(multiplexer_1_out), .in1({32{1'b0}}), .out(wb_data), .sel(RST));

  assign wb_addr = wb_addr_wb;
  assign wb_en = wb_en_wb;

  // Other names for the same wires on the sheet: current_pc_if[31:0] = current_pc; wb_data_wb[31:0] = wb_data;
  //   WBSel[1:0] = WBSel_wb
endmodule
